// Logisim project 2.circ as structural Verilog: 6 circuits, main circuit main
module main (
  input  Run_command
);

  wire _1colod, _2colod, _3colod, _4colod, _5colod, _6colod, _7colod, and_1_out, button_1_out, cancel_com,
       cdm8_done, cdm_8_mark5_1_p4, cdm_8_mark5_1_p5, Clock, com_written, command_clock, command_ld,
       comparator_1_eq, comparator_2_eq, comparator_3_eq, comparator_4_eq, comparator_5_eq, comparator_6_eq,
       comparator_7_eq, comparator_8_eq, comparator_9_eq, comparator_10_eq, comparator_11_eq,
       comparator_12_eq, comparator_13_eq, comparator_14_eq, comparator_15_eq, comparator_16_eq,
       comparator_17_eq, comparator_19_eq, comparator_20_eq, comparator_21_eq, comparator_22_eq,
       comparator_23_eq, comparator_24_eq, comparator_25_eq, comparator_26_eq, comparator_27_eq,
       comparator_28_eq, comparator_29_eq, comparator_30_eq, comparator_31_eq, comparator_32_eq,
       comparator_33_eq, comparator_34_eq, comparator_35_eq, comparator_36_eq, comparator_37_eq,
       comparator_38_eq, comparator_39_eq, comparator_40_eq, comparator_41_eq, comparator_42_eq,
       comparator_43_eq, comparator_44_eq, comparator_45_eq, comparator_46_eq, comparator_47_eq,
       comparator_48_eq, comparator_49_eq, comparator_50_eq, comparator_51_eq, comparator_52_eq,
       comparator_53_eq, comparator_54_eq, comparator_55_eq, comparator_56_eq, comparator_57_eq,
       comparator_58_eq, comparator_59_eq, comparator_60_eq, comparator_61_eq, comparator_62_eq,
       comparator_63_eq, comparator_64_eq, comparator_65_lt, comparator_67_eq, comparator_68_eq,
       comparator_69_eq, comparator_70_eq, comparator_71_eq, comparator_72_eq, comparator_73_eq,
       comparator_74_eq, comparator_75_eq, comparator_76_eq, comparator_77_eq, comparator_78_eq,
       comparator_79_eq, comparator_80_eq, controlled_buffer_4_out, controlled_buffer_6_out,
       controlled_buffer_10_out, controlled_buffer_12_out, controlled_buffer_13_out, d_ff_1_q, d_ff_2_q,
       d_ff_5_q, data_ins, data_o, do_prog, first_usage, gen_clock, gen_done, gen_ld, ins_p, IO_o, l_d,
       memory, move_done, new_com, not_1_out, not_2_out, not_3_out, not_4_out, not_5_out, not_6_out,
       not_7_out, not_8_out, not_9_out, not_10_out, not_11_out, or_1_out, or_2_out, or_3_out, or_4_out,
       or_5_out, or_7_out, print_cards_1_print, print_clock, print_done, print_ld, pull_resistor_1_node,
       pull_resistor_4_node, pull_resistor_5_node, pull_resistor_6_node, ram_clock, ram_control, ram_ld,
       read_write, register_80_q, register_82_q, reset, sent_clock, sent_done, sent_ld, shocetake, to_print,
       vector_p, write_sentinels_1_clock_gen, write_sentinels_1_l_d, zeroing;
  wire [0:0] and_2_out;
  wire [2:0] priority_encoder_1_out;
  wire [3:0] _9a, _9b, _9c, _9d, _9e, _9f, _91, _92, _93, _94, _95, _96, _97, _98, a0, a1, a2, a4, a5, a6,
       a7, a8, a9, aa, ab, ac, ad, af, b0, b1, b2, b3, b4, b5, b6, b7, b8, b9, bb, bc, bd, be, bf, c0, c1,
       c2, c3, c4, c5, c6, c8, c9, ca, cb, cc, cd, ce, cf, d0, d1, d2, d3, d4, d6, d7, d8, d9, da, db, dc,
       dd, de, df, e0, e1, e2, e3, value;
  wire [7:0] addr, card_address, card_value, cdm_8_mark5_1_p10, cdm_8_mark5_1_p11, command_address,
       command_data, controlled_buffer_3_out, controlled_buffer_5_out, controlled_buffer_9_out, counter_1_q,
       counter_2_q, current_command, data_base, gen_data, multiplexer_2_out, multiplexer_5_out,
       multiplexer_6_out, multiplexer_7_out, print_cards_1_adr, ram_data, register_79_q, register_81_q,
       register_83_q, sent_data, write_sentinels_1_address, write_sentinels_1_data;
  wire [11:0] counter_3_q;

  D_Flip_Flop d_ff_1 (.Q(d_ff_1_q), .preset(do_prog), .reset(and_1_out));  // open: clk, D, Qn, en
  and and_1 (and_1_out, not_2_out, not_1_out);
  not not_1 (not_1_out, not_2_out);
  and and_2 (and_2_out[0], addr[4], addr[5], addr[6], addr[7]);
  Comparator comparator_1 (.a(card_address), .b(8'h91), .eq(comparator_1_eq));  // open: gt, lt
  Comparator comparator_2 (.a(card_address), .b(8'h92), .eq(comparator_2_eq));  // open: gt, lt
  Comparator comparator_3 (.a(card_address), .b(8'h93), .eq(comparator_3_eq));  // open: gt, lt
  Comparator comparator_4 (.a(card_address), .b(8'h94), .eq(comparator_4_eq));  // open: gt, lt
  Comparator comparator_5 (.a(card_address), .b(8'h95), .eq(comparator_5_eq));  // open: gt, lt
  Comparator comparator_6 (.a(card_address), .b(8'h96), .eq(comparator_6_eq));  // open: gt, lt
  Comparator comparator_7 (.a(card_address), .b(8'h97), .eq(comparator_7_eq));  // open: gt, lt
  Comparator comparator_8 (.a(card_address), .b(8'h98), .eq(comparator_8_eq));  // open: gt, lt
  // Probe on cdm_8_mark5_1_p4
  // NOT_Gate not_2 has open pins: in=open, out=not_2_out
  Decoder #(.select(2), .disabled(0)) decoder_1 (
    .out0(ins_p), .out1(vector_p), .out2(data_o), .out3(IO_o), .sel({data_ins, and_2_out[0]}), .en(memory));
  D_Flip_Flop d_ff_2 (.Q(d_ff_2_q), .preset(or_1_out), .reset(not_3_out));  // open: clk, D, Qn, en
  not not_3 (not_3_out, or_1_out);
  or or_1 (or_1_out, _1colod, _2colod, _3colod, _4colod, _5colod, _6colod, _7colod);
  and and_3 (do_prog, Run_command, com_written, move_done);
  Register #(.width(4)) register_1 (.D(value), .Q(_91), .clk(comparator_1_eq));  // open: en, clr
  Register #(.width(4)) register_2 (.D(value), .Q(_92), .clk(comparator_2_eq));  // open: en, clr
  Register #(.width(4)) register_3 (.D(value), .Q(_93), .clk(comparator_3_eq));  // open: en, clr
  Register #(.width(4)) register_4 (.D(value), .Q(_94), .clk(comparator_4_eq));  // open: en, clr
  Register #(.width(4)) register_5 (.D(value), .Q(_95), .clk(comparator_5_eq));  // open: en, clr
  Register #(.width(4)) register_6 (.D(value), .Q(_96), .clk(comparator_6_eq));  // open: en, clr
  Register #(.width(4)) register_7 (.D(value), .Q(_97), .clk(comparator_7_eq));  // open: en, clr
  Register #(.width(4)) register_8 (.D(value), .Q(_98), .clk(comparator_8_eq));  // open: en, clr
  // Probe on cdm_8_mark5_1_p5
  Clock clock_1 (.out(Clock));
  Counter counter_1 (.Q(counter_1_q), .clk(d_ff_2_q), .clr(zeroing));  // open: load, D, count, carry
  Comparator comparator_9 (.a(card_address), .b(8'h9a), .eq(comparator_9_eq));  // open: gt, lt
  Comparator comparator_10 (.a(card_address), .b(8'h9b), .eq(comparator_10_eq));  // open: gt, lt
  Comparator comparator_11 (.a(card_address), .b(8'h9c), .eq(comparator_11_eq));  // open: gt, lt
  Comparator comparator_12 (.a(card_address), .b(8'h9d), .eq(comparator_12_eq));  // open: gt, lt
  Comparator comparator_13 (.a(card_address), .b(8'h9e), .eq(comparator_13_eq));  // open: gt, lt
  Comparator comparator_14 (.a(card_address), .b(8'h9f), .eq(comparator_14_eq));  // open: gt, lt
  Comparator comparator_15 (.a(card_address), .b(8'ha0), .eq(comparator_15_eq));  // open: gt, lt
  Comparator comparator_16 (.a(card_address), .b(8'ha1), .eq(comparator_16_eq));  // open: gt, lt
  Comparator comparator_17 (.a(card_address), .b(8'ha2), .eq(comparator_17_eq));  // open: gt, lt
  // CdM_8_mark5 cdm_8_mark5_1: pin names not known; wires that end beside it: d_ff_1_q, 3'b000, Clock, cdm_8_mark5_1_p4, cdm_8_mark5_1_p5, data_ins, memory, read_write, addr, cdm_8_mark5_1_p10, cdm_8_mark5_1_p11
  assign cdm_8_mark5_1_p11 = read_write ? data_base : 8'bz;  // Controlled_Buffer controlled_buffer_1
  Comparator #(.mode("unsigned")) comparator_18 (.a(counter_1_q), .b({8{1'b0}}), .eq(first_usage));  // open: gt, lt
  Register #(.width(4)) register_9 (.D(value), .Q(_9a), .clk(comparator_9_eq));  // open: en, clr
  Register #(.width(4)) register_10 (.D(value), .Q(_9b), .clk(comparator_10_eq));  // open: en, clr
  Register #(.width(4)) register_11 (.D(value), .Q(_9c), .clk(comparator_11_eq));  // open: en, clr
  Register #(.width(4)) register_12 (.D(value), .Q(_9d), .clk(comparator_12_eq));  // open: en, clr
  Register #(.width(4)) register_13 (.D(value), .Q(_9e), .clk(comparator_13_eq));  // open: en, clr
  Register #(.width(4)) register_14 (.D(value), .Q(_9f), .clk(comparator_14_eq));  // open: en, clr
  Register #(.width(4)) register_15 (.D(value), .Q(a0), .clk(comparator_15_eq));  // open: en, clr
  Register #(.width(4)) register_16 (.D(value), .Q(a1), .clk(comparator_16_eq));  // open: en, clr
  Register #(.width(4)) register_17 (.D(value), .Q(a2), .clk(comparator_17_eq));  // open: en, clr
  Multiplexer #(.width(4), .enable("false")) multiplexer_1 (
    .in0(card_value[3:0]), .in1(4'b1100), .out(value), .sel(card_value[7]));
  assign data_base = not_4_out ? cdm_8_mark5_1_p10 : 8'bz;  // Controlled_Buffer controlled_buffer_2
  not not_4 (not_4_out, read_write);
  or or_2 (or_2_out, ins_p, vector_p);
  Register #(.width(4)) register_18 (.D(value), .Q(a4), .clk(comparator_19_eq));  // open: en, clr
  Comparator comparator_19 (.a(card_address), .b(8'ha4), .eq(comparator_19_eq));  // open: gt, lt
  Register #(.width(4)) register_19 (.D(value), .Q(a5), .clk(comparator_20_eq));  // open: en, clr
  Comparator comparator_20 (.a(card_address), .b(8'ha5), .eq(comparator_20_eq));  // open: gt, lt
  Register #(.width(4)) register_20 (.D(value), .Q(a6), .clk(comparator_21_eq));  // open: en, clr
  Comparator comparator_21 (.a(card_address), .b(8'ha6), .eq(comparator_21_eq));  // open: gt, lt
  Register #(.width(4)) register_21 (.D(value), .Q(a7), .clk(comparator_22_eq));  // open: en, clr
  Comparator comparator_22 (.a(card_address), .b(8'ha7), .eq(comparator_22_eq));  // open: gt, lt
  Register #(.width(4)) register_22 (.D(value), .Q(a8), .clk(comparator_23_eq));  // open: en, clr
  Comparator comparator_23 (.a(card_address), .b(8'ha8), .eq(comparator_23_eq));  // open: gt, lt
  Register #(.width(4)) register_23 (.D(value), .Q(a9), .clk(comparator_24_eq));  // open: en, clr
  Comparator comparator_24 (.a(card_address), .b(8'ha9), .eq(comparator_24_eq));  // open: gt, lt
  Register #(.width(4)) register_24 (.D(value), .Q(aa), .clk(comparator_25_eq));  // open: en, clr
  Comparator comparator_25 (.a(card_address), .b(8'haa), .eq(comparator_25_eq));  // open: gt, lt
  Register #(.width(4)) register_25 (.D(value), .Q(ab), .clk(comparator_26_eq));  // open: en, clr
  Comparator comparator_26 (.a(card_address), .b(8'hab), .eq(comparator_26_eq));  // open: gt, lt
  Register #(.width(4)) register_26 (.D(value), .Q(ac), .clk(comparator_27_eq));  // open: en, clr
  Comparator comparator_27 (.a(card_address), .b(8'hac), .eq(comparator_27_eq));  // open: gt, lt
  Register #(.width(4)) register_27 (.D(value), .Q(ad), .clk(comparator_28_eq));  // open: en, clr
  Comparator comparator_28 (.a(card_address), .b(8'had), .eq(comparator_28_eq));  // open: gt, lt
  ROM rom_1 (.addr(addr), .data(data_base), .sel(or_2_out));
  D_Flip_Flop d_ff_3 (.clk(Clock), .D(or_3_out), .Q(zeroing));  // open: Qn, preset, en, reset
  or or_3 (or_3_out, reset, cancel_com, cdm8_done);
  not not_5 (not_5_out, ram_control);
  or or_4 (or_4_out, data_o, not_5_out, IO_o, data_ins);
  Register #(.width(4)) register_28 (.D(value), .Q(af), .clk(comparator_29_eq));  // open: en, clr
  Comparator comparator_29 (.a(card_address), .b(8'haf), .eq(comparator_29_eq));  // open: gt, lt
  Register #(.width(4)) register_29 (.D(value), .Q(b0), .clk(comparator_30_eq));  // open: en, clr
  Comparator comparator_30 (.a(card_address), .b(8'hb0), .eq(comparator_30_eq));  // open: gt, lt
  Register #(.width(4)) register_30 (.D(value), .Q(b1), .clk(comparator_31_eq));  // open: en, clr
  Comparator comparator_31 (.a(card_address), .b(8'hb1), .eq(comparator_31_eq));  // open: gt, lt
  Register #(.width(4)) register_31 (.D(value), .Q(b2), .clk(comparator_32_eq));  // open: en, clr
  Comparator comparator_32 (.a(card_address), .b(8'hb2), .eq(comparator_32_eq));  // open: gt, lt
  Register #(.width(4)) register_32 (.D(value), .Q(b3), .clk(comparator_33_eq));  // open: en, clr
  Comparator comparator_33 (.a(card_address), .b(8'hb3), .eq(comparator_33_eq));  // open: gt, lt
  Register #(.width(4)) register_33 (.D(value), .Q(b4), .clk(comparator_34_eq));  // open: en, clr
  Comparator comparator_34 (.a(card_address), .b(8'hb4), .eq(comparator_34_eq));  // open: gt, lt
  Register #(.width(4)) register_34 (.D(value), .Q(b5), .clk(comparator_35_eq));  // open: en, clr
  Comparator comparator_35 (.a(card_address), .b(8'hb5), .eq(comparator_35_eq));  // open: gt, lt
  Register #(.width(4)) register_35 (.D(value), .Q(b6), .clk(comparator_36_eq));  // open: en, clr
  Comparator comparator_36 (.a(card_address), .b(8'hb6), .eq(comparator_36_eq));  // open: gt, lt
  Register #(.width(4)) register_36 (.D(value), .Q(b7), .clk(comparator_37_eq));  // open: en, clr
  Comparator comparator_37 (.a(card_address), .b(8'hb7), .eq(comparator_37_eq));  // open: gt, lt
  Register #(.width(4)) register_37 (.D(value), .Q(b8), .clk(comparator_38_eq));  // open: en, clr
  Comparator comparator_38 (.a(card_address), .b(8'hb8), .eq(comparator_38_eq));  // open: gt, lt
  Register #(.width(4)) register_38 (.D(value), .Q(b9), .clk(comparator_39_eq));  // open: en, clr
  Comparator comparator_39 (.a(card_address), .b(8'hb9), .eq(comparator_39_eq));  // open: gt, lt
  Multiplexer #(.width(8), .enable("false")) multiplexer_2 (
    .in0(command_address), .in1(addr), .out(multiplexer_2_out), .sel(ram_control));
  or or_5 (or_5_out, first_usage, cdm8_done);
  Pull_Resistor pull_resistor_1 (.node(pull_resistor_1_node));
  Pull_Resistor pull_resistor_2 (.node(l_d));
  Multiplexer #(.enable("false")) multiplexer_3 (
    .in0(ram_clock), .in1(Clock), .out(pull_resistor_1_node), .sel(ram_control));
  and and_4 (to_print, or_5_out, sent_done);
  Comparator comparator_40 (.a(card_address), .b(8'hbb), .eq(comparator_40_eq));  // open: gt, lt
  Comparator comparator_41 (.a(card_address), .b(8'hbc), .eq(comparator_41_eq));  // open: gt, lt
  Comparator comparator_42 (.a(card_address), .b(8'hbd), .eq(comparator_42_eq));  // open: gt, lt
  Comparator comparator_43 (.a(card_address), .b(8'hbe), .eq(comparator_43_eq));  // open: gt, lt
  Comparator comparator_44 (.a(card_address), .b(8'hbf), .eq(comparator_44_eq));  // open: gt, lt
  Comparator comparator_45 (.a(card_address), .b(8'hc0), .eq(comparator_45_eq));  // open: gt, lt
  Comparator comparator_46 (.a(card_address), .b(8'hc1), .eq(comparator_46_eq));  // open: gt, lt
  Comparator comparator_47 (.a(card_address), .b(8'hc2), .eq(comparator_47_eq));  // open: gt, lt
  Comparator comparator_48 (.a(card_address), .b(8'hc3), .eq(comparator_48_eq));  // open: gt, lt
  Comparator comparator_49 (.a(card_address), .b(8'hc4), .eq(comparator_49_eq));  // open: gt, lt
  Comparator comparator_50 (.a(card_address), .b(8'hc5), .eq(comparator_50_eq));  // open: gt, lt
  Comparator comparator_51 (.a(card_address), .b(8'hc6), .eq(comparator_51_eq));  // open: gt, lt
  assign controlled_buffer_3_out = not_6_out ? multiplexer_5_out : 8'bz;  // Controlled_Buffer controlled_buffer_3
  RAM ram_1 (
    .addr(multiplexer_2_out), .data(controlled_buffer_3_out), .sel(or_4_out), .clk(pull_resistor_1_node),
    .ld(l_d), .clr(reset));
  not not_6 (not_6_out, l_d);
  Multiplexer #(.enable("false")) multiplexer_4 (.in0(ram_ld), .in1(read_write), .out(l_d), .sel(ram_control));
  Counter counter_2 (.Q(counter_2_q), .clk(controlled_buffer_4_out), .clr(reset));  // open: load, D, count, carry
  assign controlled_buffer_4_out = comparator_65_lt ? Clock : 1'bz;  // Controlled_Buffer controlled_buffer_4
  D_Flip_Flop d_ff_4 (.clk(com_written), .D(com_written), .Q(shocetake), .reset(cdm8_done));  // open: Qn, preset, en
  Register #(.width(4)) register_39 (.D(value), .Q(bb), .clk(comparator_40_eq));  // open: en, clr
  Register #(.width(4)) register_40 (.D(value), .Q(bc), .clk(comparator_41_eq));  // open: en, clr
  Register #(.width(4)) register_41 (.D(value), .Q(bd), .clk(comparator_42_eq));  // open: en, clr
  Register #(.width(4)) register_42 (.D(value), .Q(be), .clk(comparator_43_eq));  // open: en, clr
  Register #(.width(4)) register_43 (.D(value), .Q(bf), .clk(comparator_44_eq));  // open: en, clr
  Register #(.width(4)) register_44 (.D(value), .Q(c0), .clk(comparator_45_eq));  // open: en, clr
  Register #(.width(4)) register_45 (.D(value), .Q(c1), .clk(comparator_46_eq));  // open: en, clr
  Register #(.width(4)) register_46 (.D(value), .Q(c2), .clk(comparator_47_eq));  // open: en, clr
  Register #(.width(4)) register_47 (.D(value), .Q(c3), .clk(comparator_48_eq));  // open: en, clr
  Register #(.width(4)) register_48 (.D(value), .Q(c4), .clk(comparator_49_eq));  // open: en, clr
  Register #(.width(4)) register_49 (.D(value), .Q(c5), .clk(comparator_50_eq));  // open: en, clr
  Register #(.width(4)) register_50 (.D(value), .Q(c6), .clk(comparator_51_eq));  // open: en, clr
  Demultiplexer #(.width(8), .tristate("true"), .enable("false")) demultiplexer_1 (
    .out0(card_value), .out1(data_base), .in(controlled_buffer_5_out), .sel(ram_control));
  assign controlled_buffer_5_out = l_d ? controlled_buffer_3_out : 8'bz;  // Controlled_Buffer controlled_buffer_5
  Multiplexer #(.width(8), .enable("false")) multiplexer_5 (
    .in0(ram_data), .in1(data_base), .out(multiplexer_5_out), .sel(ram_control));
  Comparator comparator_52 (.a(card_address), .b(8'hc8), .eq(comparator_52_eq));  // open: gt, lt
  Comparator comparator_53 (.a(card_address), .b(8'hc9), .eq(comparator_53_eq));  // open: gt, lt
  Comparator comparator_54 (.a(card_address), .b(8'hca), .eq(comparator_54_eq));  // open: gt, lt
  Comparator comparator_55 (.a(card_address), .b(8'hcb), .eq(comparator_55_eq));  // open: gt, lt
  Comparator comparator_56 (.a(card_address), .b(8'hcc), .eq(comparator_56_eq));  // open: gt, lt
  Comparator comparator_57 (.a(card_address), .b(8'hcd), .eq(comparator_57_eq));  // open: gt, lt
  Comparator comparator_58 (.a(card_address), .b(8'hce), .eq(comparator_58_eq));  // open: gt, lt
  Comparator comparator_59 (.a(card_address), .b(8'hcf), .eq(comparator_59_eq));  // open: gt, lt
  Comparator comparator_60 (.a(card_address), .b(8'hd0), .eq(comparator_60_eq));  // open: gt, lt
  Comparator comparator_61 (.a(card_address), .b(8'hd1), .eq(comparator_61_eq));  // open: gt, lt
  Comparator comparator_62 (.a(card_address), .b(8'hd2), .eq(comparator_62_eq));  // open: gt, lt
  Comparator comparator_63 (.a(card_address), .b(8'hd3), .eq(comparator_63_eq));  // open: gt, lt
  Comparator comparator_64 (.a(card_address), .b(8'hd4), .eq(comparator_64_eq));  // open: gt, lt
  Comparator #(.mode("unsigned")) comparator_65 (.a(counter_2_q), .b(8'h1f), .lt(comparator_65_lt));  // open: gt, eq
  assign controlled_buffer_6_out = shocetake ? Clock : 1'bz;  // Controlled_Buffer controlled_buffer_6
  Register #(.width(4)) register_51 (.D(value), .Q(c8), .clk(comparator_52_eq));  // open: en, clr
  Register #(.width(4)) register_52 (.D(value), .Q(c9), .clk(comparator_53_eq));  // open: en, clr
  Register #(.width(4)) register_53 (.D(value), .Q(ca), .clk(comparator_54_eq));  // open: en, clr
  Register #(.width(4)) register_54 (.D(value), .Q(cb), .clk(comparator_55_eq));  // open: en, clr
  Register #(.width(4)) register_55 (.D(value), .Q(cc), .clk(comparator_56_eq));  // open: en, clr
  Register #(.width(4)) register_56 (.D(value), .Q(cd), .clk(comparator_57_eq));  // open: en, clr
  Register #(.width(4)) register_57 (.D(value), .Q(ce), .clk(comparator_58_eq));  // open: en, clr
  Register #(.width(4)) register_58 (.D(value), .Q(cf), .clk(comparator_59_eq));  // open: en, clr
  Register #(.width(4)) register_59 (.D(value), .Q(d0), .clk(comparator_60_eq));  // open: en, clr
  Register #(.width(4)) register_60 (.D(value), .Q(d1), .clk(comparator_61_eq));  // open: en, clr
  Register #(.width(4)) register_61 (.D(value), .Q(d2), .clk(comparator_62_eq));  // open: en, clr
  Register #(.width(4)) register_62 (.D(value), .Q(d3), .clk(comparator_63_eq));  // open: en, clr
  Register #(.width(4)) register_63 (.D(value), .Q(d4), .clk(comparator_64_eq));  // open: en, clr
  or or_6 (ram_control, shocetake, comparator_65_lt);
  D_Flip_Flop d_ff_5 (.clk(Run_command), .D(Run_command), .Q(d_ff_5_q), .reset(cdm8_done));  // open: Qn, preset, en
  Counter #(.width(12), .max('hfff)) counter_3 (
    .Q(counter_3_q), .clk(controlled_buffer_6_out), .clr(cdm8_done));  // open: load, D, count, carry
  D_Flip_Flop d_ff_6 (.clk(Clock), .D(d_ff_5_q), .Q(com_written), .reset(cdm8_done));  // open: Qn, preset, en
  Comparator #(.width(12), .mode("unsigned")) comparator_66 (
    .a(counter_3_q), .b(12'hff), .eq(cdm8_done));  // open: gt, lt
  Register #(.width(4)) register_64 (.D(value), .Q(d6), .clk(comparator_67_eq));  // open: en, clr
  Comparator comparator_67 (.a(card_address), .b(8'hd6), .eq(comparator_67_eq));  // open: gt, lt
  Register #(.width(4)) register_65 (.D(value), .Q(d7), .clk(comparator_68_eq));  // open: en, clr
  Comparator comparator_68 (.a(card_address), .b(8'hd7), .eq(comparator_68_eq));  // open: gt, lt
  Register #(.width(4)) register_66 (.D(value), .Q(d8), .clk(comparator_69_eq));  // open: en, clr
  Comparator comparator_69 (.a(card_address), .b(8'hd8), .eq(comparator_69_eq));  // open: gt, lt
  Register #(.width(4)) register_67 (.D(value), .Q(d9), .clk(comparator_70_eq));  // open: en, clr
  Comparator comparator_70 (.a(card_address), .b(8'hd9), .eq(comparator_70_eq));  // open: gt, lt
  Register #(.width(4)) register_68 (.D(value), .Q(da), .clk(comparator_71_eq));  // open: en, clr
  Comparator comparator_71 (.a(card_address), .b(8'hda), .eq(comparator_71_eq));  // open: gt, lt
  Register #(.width(4)) register_69 (.D(value), .Q(db), .clk(comparator_72_eq));  // open: en, clr
  Comparator comparator_72 (.a(card_address), .b(8'hdb), .eq(comparator_72_eq));  // open: gt, lt
  Register #(.width(4)) register_70 (.D(value), .Q(dc), .clk(comparator_73_eq));  // open: en, clr
  Comparator comparator_73 (.a(card_address), .b(8'hdc), .eq(comparator_73_eq));  // open: gt, lt
  Register #(.width(4)) register_71 (.D(value), .Q(dd), .clk(comparator_74_eq));  // open: en, clr
  Comparator comparator_74 (.a(card_address), .b(8'hdd), .eq(comparator_74_eq));  // open: gt, lt
  Register #(.width(4)) register_72 (.D(value), .Q(de), .clk(comparator_75_eq));  // open: en, clr
  Comparator comparator_75 (.a(card_address), .b(8'hde), .eq(comparator_75_eq));  // open: gt, lt
  Register #(.width(4)) register_73 (.D(value), .Q(df), .clk(comparator_76_eq));  // open: en, clr
  Comparator comparator_76 (.a(card_address), .b(8'hdf), .eq(comparator_76_eq));  // open: gt, lt
  Register #(.width(4)) register_74 (.D(value), .Q(e0), .clk(comparator_77_eq));  // open: en, clr
  Comparator comparator_77 (.a(card_address), .b(8'he0), .eq(comparator_77_eq));  // open: gt, lt
  Register #(.width(4)) register_75 (.D(value), .Q(e1), .clk(comparator_78_eq));  // open: en, clr
  Comparator comparator_78 (.a(card_address), .b(8'he1), .eq(comparator_78_eq));  // open: gt, lt
  Register #(.width(4)) register_76 (.D(value), .Q(e2), .clk(comparator_79_eq));  // open: en, clr
  Comparator comparator_79 (.a(card_address), .b(8'he2), .eq(comparator_79_eq));  // open: gt, lt
  Register #(.width(4)) register_77 (.D(value), .Q(e3), .clk(comparator_80_eq));  // open: en, clr
  Comparator comparator_80 (.a(card_address), .b(8'he3), .eq(comparator_80_eq));  // open: gt, lt
  not not_7 (not_7_out, not_7_out);
  not not_8 (not_8_out, not_8_out);
  Button button_1 (.out(button_1_out));
  Hex_Digit_Display hex_digit_display_1 (.value(current_command[7:4]));  // open: dp
  assign ram_data = gen_data;  // Buffer buffer_1, 8 bits wide
  assign ram_data = sent_data;  // Buffer buffer_2, 8 bits wide
  assign ram_data = command_data;  // Buffer buffer_3, 8 bits wide
  Button button_2 (.out(reset));
  Button button_3 (.out(cancel_com));
  Hex_Digit_Display hex_digit_display_2 (.value(current_command[3:0]));  // open: dp
  Register register_78 (.D(multiplexer_6_out), .Q(card_address), .clk(print_clock));  // open: en, clr
  Multiplexer #(.width(8), .enable("false")) multiplexer_6 (
    .in0({8{1'b1}}), .in1(command_address), .out(multiplexer_6_out), .sel(to_print));
  Priority_Encoder priority_encoder_1 (
    .in0(1'b0), .in1(_1colod), .in2(_2colod), .in3(_3colod), .in4(_4colod), .in5(_5colod), .in6(_6colod),
    .in7(_7colod), .out(priority_encoder_1_out), .gs(new_com));  // open: en_in, en_out
  Multiplexer #(.width(8), .enable("false")) multiplexer_7 (
    .in0(current_command), .in1({8{1'b0}}), .out(multiplexer_7_out), .sel(zeroing));
  Pull_Resistor pull_resistor_3 (.node(priority_encoder_1_out));
  Register register_79 (.D(multiplexer_7_out), .Q(register_79_q), .clk(Clock));  // open: en, clr
  Button button_4 (.out(_1colod));
  Hex_Digit_Display hex_digit_display_3 (.value(_91));  // open: dp
  Hex_Digit_Display hex_digit_display_4 (.value(_92));  // open: dp
  Hex_Digit_Display hex_digit_display_5 (.value(_93));  // open: dp
  Hex_Digit_Display hex_digit_display_6 (.value(_94));  // open: dp
  Hex_Digit_Display hex_digit_display_7 (.value(_95));  // open: dp
  Hex_Digit_Display hex_digit_display_8 (.value(_96));  // open: dp
  Hex_Digit_Display hex_digit_display_9 (.value(_97));  // open: dp
  Hex_Digit_Display hex_digit_display_10 (.value(_98));  // open: dp
  buf buffer_4 (ram_clock, gen_clock);
  buf buffer_5 (ram_clock, sent_clock);
  buf buffer_6 (ram_clock, print_clock);
  buf buffer_7 (ram_clock, command_clock);
  card_replace card_replace_1 (
    .colod_number(priority_encoder_1_out), .cur_command(register_79_q), .updated_program(current_command),
    .move_done_updated(move_done));
  Button button_5 (.out(_2colod));
  Hex_Digit_Display hex_digit_display_11 (.value(_9a));  // open: dp
  Hex_Digit_Display hex_digit_display_12 (.value(_9b));  // open: dp
  Hex_Digit_Display hex_digit_display_13 (.value(_9c));  // open: dp
  Hex_Digit_Display hex_digit_display_14 (.value(_9d));  // open: dp
  Hex_Digit_Display hex_digit_display_15 (.value(_9e));  // open: dp
  Hex_Digit_Display hex_digit_display_16 (.value(_9f));  // open: dp
  Hex_Digit_Display hex_digit_display_17 (.value(a0));  // open: dp
  Hex_Digit_Display hex_digit_display_18 (.value(a1));  // open: dp
  Hex_Digit_Display hex_digit_display_19 (.value(a2));  // open: dp
  buf buffer_8 (ram_ld, gen_ld);
  buf buffer_9 (ram_ld, sent_ld);
  buf buffer_10 (ram_ld, print_ld);
  buf buffer_11 (ram_ld, command_ld);
  Hex_Digit_Display hex_digit_display_20 (.value(a4));  // open: dp
  Hex_Digit_Display hex_digit_display_21 (.value(a5));  // open: dp
  Hex_Digit_Display hex_digit_display_22 (.value(a6));  // open: dp
  Hex_Digit_Display hex_digit_display_23 (.value(a7));  // open: dp
  Hex_Digit_Display hex_digit_display_24 (.value(a8));  // open: dp
  Hex_Digit_Display hex_digit_display_25 (.value(a9));  // open: dp
  Hex_Digit_Display hex_digit_display_26 (.value(aa));  // open: dp
  Hex_Digit_Display hex_digit_display_27 (.value(ab));  // open: dp
  Hex_Digit_Display hex_digit_display_28 (.value(ac));  // open: dp
  Hex_Digit_Display hex_digit_display_29 (.value(ad));  // open: dp
  not not_9 (not_9_out, print_done);
  assign command_address = not_9_out ? controlled_buffer_9_out : 8'bz;  // Controlled_Buffer controlled_buffer_7
  assign print_clock = not_9_out ? controlled_buffer_10_out : 1'bz;  // Controlled_Buffer controlled_buffer_8
  Button button_6 (.out(_3colod));
  assign controlled_buffer_9_out = to_print ? print_cards_1_adr : 8'bz;  // Controlled_Buffer controlled_buffer_9
  Pull_Resistor pull_resistor_4 (.node(pull_resistor_4_node));
  assign controlled_buffer_10_out = to_print ? pull_resistor_4_node : 1'bz;  // Controlled_Buffer controlled_buffer_10
  assign pull_resistor_4_node = to_print ? Clock : 1'bz;  // Controlled_Buffer controlled_buffer_11
  assign controlled_buffer_12_out = register_80_q ? Clock : 1'bz;  // Controlled_Buffer controlled_buffer_12
  Register #(.width(1)) register_80 (.D(1'b1), .Q(register_80_q), .clk(Run_command), .clr(cdm8_done));  // open: en
  Button button_7 (.out(_4colod));
  Hex_Digit_Display hex_digit_display_30 (.value(af));  // open: dp
  Hex_Digit_Display hex_digit_display_31 (.value(b0));  // open: dp
  Hex_Digit_Display hex_digit_display_32 (.value(b1));  // open: dp
  Hex_Digit_Display hex_digit_display_33 (.value(b2));  // open: dp
  Hex_Digit_Display hex_digit_display_34 (.value(b3));  // open: dp
  Hex_Digit_Display hex_digit_display_35 (.value(b4));  // open: dp
  Hex_Digit_Display hex_digit_display_36 (.value(b5));  // open: dp
  Hex_Digit_Display hex_digit_display_37 (.value(b6));  // open: dp
  Hex_Digit_Display hex_digit_display_38 (.value(b7));  // open: dp
  Hex_Digit_Display hex_digit_display_39 (.value(b8));  // open: dp
  Hex_Digit_Display hex_digit_display_40 (.value(b9));  // open: dp
  print_cards print_cards_1 (
    .clock(pull_resistor_4_node), .adr(print_cards_1_adr), .print(print_cards_1_print), .move_done(or_7_out),
    .print_done(print_done));
  assign controlled_buffer_13_out = to_print ? print_cards_1_print : 1'bz;  // Controlled_Buffer controlled_buffer_13
  or or_7 (or_7_out, cdm8_done, reset);
  Register register_81 (.D(current_command), .Q(register_81_q), .clk(Run_command));  // open: en, clr
  assign command_data = print_done ? register_81_q : 8'bz;  // Controlled_Buffer controlled_buffer_14
  assign command_clock = print_done ? controlled_buffer_12_out : 1'bz;  // Controlled_Buffer controlled_buffer_15
  Button button_8 (.out(_5colod));
  Hex_Digit_Display hex_digit_display_41 (.value(bb));  // open: dp
  Hex_Digit_Display hex_digit_display_42 (.value(bc));  // open: dp
  Hex_Digit_Display hex_digit_display_43 (.value(bd));  // open: dp
  Hex_Digit_Display hex_digit_display_44 (.value(be));  // open: dp
  Hex_Digit_Display hex_digit_display_45 (.value(bf));  // open: dp
  Hex_Digit_Display hex_digit_display_46 (.value(c0));  // open: dp
  Hex_Digit_Display hex_digit_display_47 (.value(c1));  // open: dp
  Hex_Digit_Display hex_digit_display_48 (.value(c2));  // open: dp
  Hex_Digit_Display hex_digit_display_49 (.value(c3));  // open: dp
  Hex_Digit_Display hex_digit_display_50 (.value(c4));  // open: dp
  Hex_Digit_Display hex_digit_display_51 (.value(c5));  // open: dp
  Hex_Digit_Display hex_digit_display_52 (.value(c6));  // open: dp
  assign sent_clock = gen_done ? write_sentinels_1_clock_gen : 1'bz;  // Controlled_Buffer controlled_buffer_16
  assign command_address = gen_done ? write_sentinels_1_address : 8'bz;  // Controlled_Buffer controlled_buffer_17
  Pull_Resistor pull_resistor_5 (.node(pull_resistor_5_node));
  assign pull_resistor_5_node = gen_done ? Clock : 1'bz;  // Controlled_Buffer controlled_buffer_18
  not not_10 (not_10_out, print_done);
  assign print_ld = not_10_out ? controlled_buffer_13_out : 1'bz;  // Controlled_Buffer controlled_buffer_19
  Button button_9 (.out(_6colod));
  Hex_Digit_Display hex_digit_display_53 (.value(c8));  // open: dp
  Hex_Digit_Display hex_digit_display_54 (.value(c9));  // open: dp
  Hex_Digit_Display hex_digit_display_55 (.value(ca));  // open: dp
  Hex_Digit_Display hex_digit_display_56 (.value(cb));  // open: dp
  Hex_Digit_Display hex_digit_display_57 (.value(cc));  // open: dp
  Hex_Digit_Display hex_digit_display_58 (.value(cd));  // open: dp
  Hex_Digit_Display hex_digit_display_59 (.value(ce));  // open: dp
  Hex_Digit_Display hex_digit_display_60 (.value(cf));  // open: dp
  Hex_Digit_Display hex_digit_display_61 (.value(d0));  // open: dp
  Hex_Digit_Display hex_digit_display_62 (.value(d1));  // open: dp
  Hex_Digit_Display hex_digit_display_63 (.value(d2));  // open: dp
  Hex_Digit_Display hex_digit_display_64 (.value(d3));  // open: dp
  Hex_Digit_Display hex_digit_display_65 (.value(d4));  // open: dp
  assign sent_ld = gen_done ? write_sentinels_1_l_d : 1'bz;  // Controlled_Buffer controlled_buffer_20
  write_sentinels write_sentinels_1 (
    .data(write_sentinels_1_data), .clock(pull_resistor_5_node), .reset(reset),
    .address(write_sentinels_1_address), .clock_gen(write_sentinels_1_clock_gen),
    .l_d(write_sentinels_1_l_d), .sent_writing_done(sent_done));
  Hex_Digit_Display hex_digit_display_66 (.value(d6));  // open: dp
  Hex_Digit_Display hex_digit_display_67 (.value(d7));  // open: dp
  Hex_Digit_Display hex_digit_display_68 (.value(d8));  // open: dp
  Hex_Digit_Display hex_digit_display_69 (.value(d9));  // open: dp
  Hex_Digit_Display hex_digit_display_70 (.value(da));  // open: dp
  Hex_Digit_Display hex_digit_display_71 (.value(db));  // open: dp
  Hex_Digit_Display hex_digit_display_72 (.value(dc));  // open: dp
  Hex_Digit_Display hex_digit_display_73 (.value(dd));  // open: dp
  Hex_Digit_Display hex_digit_display_74 (.value(de));  // open: dp
  Hex_Digit_Display hex_digit_display_75 (.value(df));  // open: dp
  Hex_Digit_Display hex_digit_display_76 (.value(e0));  // open: dp
  Hex_Digit_Display hex_digit_display_77 (.value(e1));  // open: dp
  Hex_Digit_Display hex_digit_display_78 (.value(e2));  // open: dp
  Hex_Digit_Display hex_digit_display_79 (.value(e3));  // open: dp
  assign sent_data = gen_done ? write_sentinels_1_data : 8'bz;  // Controlled_Buffer controlled_buffer_21
  generator generator_1 (
    .clock(pull_resistor_6_node), .reset(reset), .data(gen_data), .address(command_address),
    .clock_gen(gen_clock), .l_d(gen_ld), .gen_done(gen_done));
  Pull_Resistor pull_resistor_6 (.node(pull_resistor_6_node));
  assign pull_resistor_6_node = not_11_out ? Clock : 1'bz;  // Controlled_Buffer controlled_buffer_22
  not not_11 (not_11_out, ram_control);
  Register #(.width(1)) register_82 (.D(1'b0), .Q(register_82_q), .clk(Run_command));  // open: en, clr
  assign command_ld = print_done ? register_82_q : 1'bz;  // Controlled_Buffer controlled_buffer_23
  assign command_address = print_done ? register_83_q : 8'bz;  // Controlled_Buffer controlled_buffer_24
  Register register_83 (.D(8'hf3), .Q(register_83_q), .clk(Run_command));  // open: en, clr
  Button button_10 (.out(_7colod));

  // Other names for the same wires on the sheet: run_com = Run_command; gen_address[7:0] = command_address;
  //   print_address[7:0] = command_address; ram_address[7:0] = command_address; sent_address[7:0] = command_address

  // Notes on the sheet:
  //   Check for the first usage of command
  //   Allows cdm8 connection after
  //   writing command
  //   Value reading
  //   Nullify all registers after
  //   completing command
  //   contents of rom_1 (hex, n*v repeats v):
  //   c1 d1 8 c1 d1 80 c1 d9 c5 d5 ee 9 d0 ff c1 d1 14 a4 c5 cd 0 d9 d2 f3 ba d0 f 42 d6 62 d0 40 bd 41 e0
  //   27 8f ee 20 c3 8b bd d2 f3 ba 4*9a d6 62 d0 f 41 89 89 e1 3c ee c 8d be 42 e1 43 ee c 76 e0 49 8f ee
  //   3d d0 7f 8b be 42 ae 8f c5 d0 40 be 42 e0 60 be a6 d2 0 ae 8f 8d ee 53 ee c d3 80 8a 1b bf d0 80 8f
  //   be 42 e0 70 ee 69 d7 15*0 90 99 a3 ae ba c7 d5 105*0 16
  //   Updating indicators
  //   Check if colod generation and adding sentinels done
  //   Controls connection to cdm8
  //   Check if command was written
  //   Checks if cdm8 finished proccess
  //   from
  //   Addresses to RAM
  //   Data to/from RAM
  //   Reset game
  //   Cancel command
  //   Current command
  //   to
  //   C - closed card
  //   0 - empty cell
  //   Card replacer
  //   Read/print to RAM
  //   RAM clock
  //   Solitaire
  //   Print cards to indicators
  //   Add sentinels
  //   Write command to RAM
  //   Generate colod
endmodule

module configuration (
  input  [31:0] colods,
  input  clock,
  output [31:0] final_colod,
  output [3:0] card
);

  wire _1, _2, _3, _4, _5, _6, _7, _8, _9, _10, _11, _12, _13, _14, _15, _16, _17, _18, _19, _20, _21, _22,
       _23, _24, _25, _26, _27, _28, _29, _30, _31, _32, bitfinder_1_found, bitfinder_2_found,
       bitfinder_3_found, bitfinder_4_found, bitfinder_5_found, bitfinder_6_found, bitfinder_7_found,
       bitfinder_8_found, bitfinder_9_found, bitfinder_10_found, bitfinder_11_found, bitfinder_12_found,
       bitfinder_13_found, bitfinder_14_found, bitfinder_15_found, bitfinder_16_found, bitfinder_17_found,
       bitfinder_18_found, bitfinder_19_found, bitfinder_20_found, bitfinder_21_found, bitfinder_22_found,
       bitfinder_23_found, bitfinder_24_found, bitfinder_25_found, bitfinder_26_found, bitfinder_27_found,
       bitfinder_28_found, bitfinder_29_found, bitfinder_30_found, bitfinder_31_found, bitfinder_32_found;
  wire [3:0] val1, val2, val3, val4, val5, val6, val7, val8, val9, val10, val11, val12, val13, val14, val15,
       val16, val17, val18, val19, val20, val21, val22, val23, val24, val25, val26, val27, val28, val29,
       val30, val31, val32;
  wire [4:0] random_1_out;
  wire [31:0] n1, n2, n3, n4, n5, n6, n7, n8, n9, n10, n11, n12, n13, n14, n15, n16, n17, n18, n19, n20, n21,
       n22, n23, n24, n25, n26, n27, n28, n29, n30, n31, n32, nor_1_out, pull_resistor_1_node,
       pull_resistor_2_node, pull_resistor_3_node, pull_resistor_4_node, pull_resistor_5_node,
       pull_resistor_6_node, pull_resistor_7_node, pull_resistor_8_node, pull_resistor_9_node,
       pull_resistor_10_node, pull_resistor_11_node, pull_resistor_12_node, pull_resistor_13_node,
       pull_resistor_14_node, pull_resistor_15_node, pull_resistor_16_node, pull_resistor_33_node,
       pull_resistor_34_node, pull_resistor_35_node, pull_resistor_36_node, pull_resistor_37_node,
       pull_resistor_38_node, pull_resistor_39_node, pull_resistor_40_node, pull_resistor_41_node,
       pull_resistor_42_node, pull_resistor_43_node, pull_resistor_44_node, pull_resistor_45_node,
       pull_resistor_46_node, pull_resistor_47_node, pull_resistor_48_node;

  Decoder #(.select(5), .enable("false")) decoder_1 (
    .out0(_1), .out1(_2), .out2(_3), .out3(_4), .out4(_5), .out5(_6), .out6(_7), .out7(_8), .out8(_9),
    .out9(_10), .out10(_11), .out11(_12), .out12(_13), .out13(_14), .out14(_15), .out15(_16), .out16(_17),
    .out17(_18), .out18(_19), .out19(_20), .out20(_21), .out21(_22), .out22(_23), .out23(_24), .out24(_25),
    .out25(_26), .out26(_27), .out27(_28), .out28(_29), .out29(_30), .out30(_31), .out31(_32),
    .sel(random_1_out));
  Random #(.width(5)) random_1 (.clk(clock), .out(random_1_out));  // open: next, clr
  Pull_Resistor pull_resistor_1 (.node(pull_resistor_1_node));
  Pull_Resistor pull_resistor_2 (.node(pull_resistor_2_node));
  Pull_Resistor pull_resistor_3 (.node(pull_resistor_3_node));
  Pull_Resistor pull_resistor_4 (.node(pull_resistor_4_node));
  Pull_Resistor pull_resistor_5 (.node(pull_resistor_5_node));
  Pull_Resistor pull_resistor_6 (.node(pull_resistor_6_node));
  Pull_Resistor pull_resistor_7 (.node(pull_resistor_7_node));
  Pull_Resistor pull_resistor_8 (.node(pull_resistor_8_node));
  Pull_Resistor pull_resistor_9 (.node(pull_resistor_9_node));
  Pull_Resistor pull_resistor_10 (.node(pull_resistor_10_node));
  Pull_Resistor pull_resistor_11 (.node(pull_resistor_11_node));
  Pull_Resistor pull_resistor_12 (.node(pull_resistor_12_node));
  Pull_Resistor pull_resistor_13 (.node(pull_resistor_13_node));
  Pull_Resistor pull_resistor_14 (.node(pull_resistor_14_node));
  Pull_Resistor pull_resistor_15 (.node(pull_resistor_15_node));
  Pull_Resistor pull_resistor_16 (.node(pull_resistor_16_node));
  assign pull_resistor_1_node = _1 ? 32'h1 : 32'bz;  // Controlled_Buffer controlled_buffer_1
  assign pull_resistor_2_node = _2 ? 32'h2 : 32'bz;  // Controlled_Buffer controlled_buffer_2
  assign pull_resistor_3_node = _3 ? 32'h4 : 32'bz;  // Controlled_Buffer controlled_buffer_3
  assign pull_resistor_4_node = _4 ? 32'h8 : 32'bz;  // Controlled_Buffer controlled_buffer_4
  assign pull_resistor_5_node = _5 ? 32'h10 : 32'bz;  // Controlled_Buffer controlled_buffer_5
  assign pull_resistor_6_node = _6 ? 32'h20 : 32'bz;  // Controlled_Buffer controlled_buffer_6
  assign pull_resistor_7_node = _7 ? 32'h40 : 32'bz;  // Controlled_Buffer controlled_buffer_7
  assign pull_resistor_8_node = _8 ? 32'h80 : 32'bz;  // Controlled_Buffer controlled_buffer_8
  assign pull_resistor_9_node = _9 ? 32'h100 : 32'bz;  // Controlled_Buffer controlled_buffer_9
  assign pull_resistor_10_node = _10 ? 32'h200 : 32'bz;  // Controlled_Buffer controlled_buffer_10
  assign pull_resistor_11_node = _11 ? 32'h400 : 32'bz;  // Controlled_Buffer controlled_buffer_11
  assign pull_resistor_12_node = _12 ? 32'h800 : 32'bz;  // Controlled_Buffer controlled_buffer_12
  assign pull_resistor_13_node = _13 ? 32'h1000 : 32'bz;  // Controlled_Buffer controlled_buffer_13
  assign pull_resistor_14_node = _14 ? 32'h2000 : 32'bz;  // Controlled_Buffer controlled_buffer_14
  assign pull_resistor_15_node = _15 ? 32'h4000 : 32'bz;  // Controlled_Buffer controlled_buffer_15
  assign pull_resistor_16_node = _16 ? 32'h8000 : 32'bz;  // Controlled_Buffer controlled_buffer_16
  assign n1 = pull_resistor_1_node & colods;  // AND_Gate and_1, 32 bits wide
  assign n2 = pull_resistor_2_node & colods;  // AND_Gate and_2, 32 bits wide
  assign n3 = pull_resistor_3_node & colods;  // AND_Gate and_3, 32 bits wide
  assign n4 = pull_resistor_4_node & colods;  // AND_Gate and_4, 32 bits wide
  assign n5 = pull_resistor_5_node & colods;  // AND_Gate and_5, 32 bits wide
  assign n6 = pull_resistor_6_node & colods;  // AND_Gate and_6, 32 bits wide
  assign n7 = pull_resistor_7_node & colods;  // AND_Gate and_7, 32 bits wide
  assign n8 = pull_resistor_8_node & colods;  // AND_Gate and_8, 32 bits wide
  assign n9 = pull_resistor_9_node & colods;  // AND_Gate and_9, 32 bits wide
  assign n10 = pull_resistor_10_node & colods;  // AND_Gate and_10, 32 bits wide
  assign n11 = pull_resistor_11_node & colods;  // AND_Gate and_11, 32 bits wide
  assign n12 = pull_resistor_12_node & colods;  // AND_Gate and_12, 32 bits wide
  assign n13 = pull_resistor_13_node & colods;  // AND_Gate and_13, 32 bits wide
  assign n14 = pull_resistor_14_node & colods;  // AND_Gate and_14, 32 bits wide
  assign n15 = pull_resistor_15_node & colods;  // AND_Gate and_15, 32 bits wide
  assign n16 = pull_resistor_16_node & colods;  // AND_Gate and_16, 32 bits wide
  BitFinder #(.width(32)) bitfinder_1 (.in(n1), .found(bitfinder_1_found));  // open: index
  BitFinder #(.width(32)) bitfinder_2 (.in(n2), .found(bitfinder_2_found));  // open: index
  BitFinder #(.width(32)) bitfinder_3 (.in(n3), .found(bitfinder_3_found));  // open: index
  BitFinder #(.width(32)) bitfinder_4 (.in(n4), .found(bitfinder_4_found));  // open: index
  BitFinder #(.width(32)) bitfinder_5 (.in(n5), .found(bitfinder_5_found));  // open: index
  BitFinder #(.width(32)) bitfinder_6 (.in(n6), .found(bitfinder_6_found));  // open: index
  BitFinder #(.width(32)) bitfinder_7 (.in(n7), .found(bitfinder_7_found));  // open: index
  BitFinder #(.width(32)) bitfinder_8 (.in(n8), .found(bitfinder_8_found));  // open: index
  BitFinder #(.width(32)) bitfinder_9 (.in(n9), .found(bitfinder_9_found));  // open: index
  BitFinder #(.width(32)) bitfinder_10 (.in(n10), .found(bitfinder_10_found));  // open: index
  BitFinder #(.width(32)) bitfinder_11 (.in(n11), .found(bitfinder_11_found));  // open: index
  BitFinder #(.width(32)) bitfinder_12 (.in(n12), .found(bitfinder_12_found));  // open: index
  BitFinder #(.width(32)) bitfinder_13 (.in(n13), .found(bitfinder_13_found));  // open: index
  BitFinder #(.width(32)) bitfinder_14 (.in(n14), .found(bitfinder_14_found));  // open: index
  BitFinder #(.width(32)) bitfinder_15 (.in(n15), .found(bitfinder_15_found));  // open: index
  BitFinder #(.width(32)) bitfinder_16 (.in(n16), .found(bitfinder_16_found));  // open: index
  Pull_Resistor pull_resistor_17 (.node(val1));
  assign val1 = bitfinder_1_found ? 4'b0010 : 4'bz;  // Controlled_Buffer controlled_buffer_17
  Pull_Resistor pull_resistor_18 (.node(val2));
  assign val2 = bitfinder_2_found ? 4'b0011 : 4'bz;  // Controlled_Buffer controlled_buffer_18
  Pull_Resistor pull_resistor_19 (.node(val3));
  assign val3 = bitfinder_3_found ? 4'b0100 : 4'bz;  // Controlled_Buffer controlled_buffer_19
  Pull_Resistor pull_resistor_20 (.node(val4));
  assign val4 = bitfinder_4_found ? 4'b0101 : 4'bz;  // Controlled_Buffer controlled_buffer_20
  Pull_Resistor pull_resistor_21 (.node(val5));
  assign val5 = bitfinder_5_found ? 4'b0110 : 4'bz;  // Controlled_Buffer controlled_buffer_21
  Pull_Resistor pull_resistor_22 (.node(val6));
  assign val6 = bitfinder_6_found ? 4'b0111 : 4'bz;  // Controlled_Buffer controlled_buffer_22
  Pull_Resistor pull_resistor_23 (.node(val7));
  assign val7 = bitfinder_7_found ? 4'b1000 : 4'bz;  // Controlled_Buffer controlled_buffer_23
  Pull_Resistor pull_resistor_24 (.node(val8));
  assign val8 = bitfinder_8_found ? 4'b1001 : 4'bz;  // Controlled_Buffer controlled_buffer_24
  Pull_Resistor pull_resistor_25 (.node(val9));
  assign val9 = bitfinder_9_found ? 4'b0010 : 4'bz;  // Controlled_Buffer controlled_buffer_25
  Pull_Resistor pull_resistor_26 (.node(val10));
  assign val10 = bitfinder_10_found ? 4'b0011 : 4'bz;  // Controlled_Buffer controlled_buffer_26
  Pull_Resistor pull_resistor_27 (.node(val11));
  assign val11 = bitfinder_11_found ? 4'b0100 : 4'bz;  // Controlled_Buffer controlled_buffer_27
  Pull_Resistor pull_resistor_28 (.node(val12));
  assign val12 = bitfinder_12_found ? 4'b0101 : 4'bz;  // Controlled_Buffer controlled_buffer_28
  Pull_Resistor pull_resistor_29 (.node(val13));
  assign val13 = bitfinder_13_found ? 4'b0110 : 4'bz;  // Controlled_Buffer controlled_buffer_29
  Pull_Resistor pull_resistor_30 (.node(val14));
  assign val14 = bitfinder_14_found ? 4'b0111 : 4'bz;  // Controlled_Buffer controlled_buffer_30
  Pull_Resistor pull_resistor_31 (.node(val15));
  assign val15 = bitfinder_15_found ? 4'b1000 : 4'bz;  // Controlled_Buffer controlled_buffer_31
  Pull_Resistor pull_resistor_32 (.node(val16));
  assign val16 = bitfinder_16_found ? 4'b1001 : 4'bz;  // Controlled_Buffer controlled_buffer_32
  Pull_Resistor pull_resistor_33 (.node(pull_resistor_33_node));
  Pull_Resistor pull_resistor_34 (.node(pull_resistor_34_node));
  Pull_Resistor pull_resistor_35 (.node(pull_resistor_35_node));
  Pull_Resistor pull_resistor_36 (.node(pull_resistor_36_node));
  Pull_Resistor pull_resistor_37 (.node(pull_resistor_37_node));
  Pull_Resistor pull_resistor_38 (.node(pull_resistor_38_node));
  Pull_Resistor pull_resistor_39 (.node(pull_resistor_39_node));
  Pull_Resistor pull_resistor_40 (.node(pull_resistor_40_node));
  Pull_Resistor pull_resistor_41 (.node(pull_resistor_41_node));
  Pull_Resistor pull_resistor_42 (.node(pull_resistor_42_node));
  Pull_Resistor pull_resistor_43 (.node(pull_resistor_43_node));
  Pull_Resistor pull_resistor_44 (.node(pull_resistor_44_node));
  Pull_Resistor pull_resistor_45 (.node(pull_resistor_45_node));
  Pull_Resistor pull_resistor_46 (.node(pull_resistor_46_node));
  Pull_Resistor pull_resistor_47 (.node(pull_resistor_47_node));
  Pull_Resistor pull_resistor_48 (.node(pull_resistor_48_node));
  assign pull_resistor_33_node = _17 ? 32'h10000 : 32'bz;  // Controlled_Buffer controlled_buffer_33
  assign n17 = pull_resistor_33_node & colods;  // AND_Gate and_17, 32 bits wide
  assign pull_resistor_34_node = _18 ? 32'h20000 : 32'bz;  // Controlled_Buffer controlled_buffer_34
  assign n18 = pull_resistor_34_node & colods;  // AND_Gate and_18, 32 bits wide
  assign pull_resistor_35_node = _19 ? 32'h40000 : 32'bz;  // Controlled_Buffer controlled_buffer_35
  assign n19 = pull_resistor_35_node & colods;  // AND_Gate and_19, 32 bits wide
  assign pull_resistor_36_node = _20 ? 32'h80000 : 32'bz;  // Controlled_Buffer controlled_buffer_36
  assign n20 = pull_resistor_36_node & colods;  // AND_Gate and_20, 32 bits wide
  assign pull_resistor_37_node = _21 ? 32'h100000 : 32'bz;  // Controlled_Buffer controlled_buffer_37
  assign n21 = pull_resistor_37_node & colods;  // AND_Gate and_21, 32 bits wide
  assign pull_resistor_38_node = _22 ? 32'h200000 : 32'bz;  // Controlled_Buffer controlled_buffer_38
  assign n22 = pull_resistor_38_node & colods;  // AND_Gate and_22, 32 bits wide
  assign pull_resistor_39_node = _23 ? 32'h400000 : 32'bz;  // Controlled_Buffer controlled_buffer_39
  assign n23 = pull_resistor_39_node & colods;  // AND_Gate and_23, 32 bits wide
  assign pull_resistor_40_node = _24 ? 32'h800000 : 32'bz;  // Controlled_Buffer controlled_buffer_40
  assign n24 = pull_resistor_40_node & colods;  // AND_Gate and_24, 32 bits wide
  assign pull_resistor_41_node = _25 ? 32'h1000000 : 32'bz;  // Controlled_Buffer controlled_buffer_41
  assign n25 = pull_resistor_41_node & colods;  // AND_Gate and_25, 32 bits wide
  assign pull_resistor_42_node = _26 ? 32'h2000000 : 32'bz;  // Controlled_Buffer controlled_buffer_42
  assign n26 = pull_resistor_42_node & colods;  // AND_Gate and_26, 32 bits wide
  assign pull_resistor_43_node = _27 ? 32'h4000000 : 32'bz;  // Controlled_Buffer controlled_buffer_43
  assign n27 = pull_resistor_43_node & colods;  // AND_Gate and_27, 32 bits wide
  assign pull_resistor_44_node = _28 ? 32'h8000000 : 32'bz;  // Controlled_Buffer controlled_buffer_44
  assign n28 = pull_resistor_44_node & colods;  // AND_Gate and_28, 32 bits wide
  assign pull_resistor_45_node = _29 ? 32'h10000000 : 32'bz;  // Controlled_Buffer controlled_buffer_45
  assign n29 = pull_resistor_45_node & colods;  // AND_Gate and_29, 32 bits wide
  assign pull_resistor_46_node = _30 ? 32'h20000000 : 32'bz;  // Controlled_Buffer controlled_buffer_46
  assign n30 = pull_resistor_46_node & colods;  // AND_Gate and_30, 32 bits wide
  assign pull_resistor_47_node = _31 ? 32'h40000000 : 32'bz;  // Controlled_Buffer controlled_buffer_47
  assign n31 = pull_resistor_47_node & colods;  // AND_Gate and_31, 32 bits wide
  assign pull_resistor_48_node = _32 ? 32'h80000000 : 32'bz;  // Controlled_Buffer controlled_buffer_48
  assign n32 = pull_resistor_48_node & colods;  // AND_Gate and_32, 32 bits wide
  BitFinder #(.width(32)) bitfinder_17 (.in(n17), .found(bitfinder_17_found));  // open: index
  BitFinder #(.width(32)) bitfinder_18 (.in(n18), .found(bitfinder_18_found));  // open: index
  BitFinder #(.width(32)) bitfinder_19 (.in(n19), .found(bitfinder_19_found));  // open: index
  BitFinder #(.width(32)) bitfinder_20 (.in(n20), .found(bitfinder_20_found));  // open: index
  BitFinder #(.width(32)) bitfinder_21 (.in(n21), .found(bitfinder_21_found));  // open: index
  BitFinder #(.width(32)) bitfinder_22 (.in(n22), .found(bitfinder_22_found));  // open: index
  BitFinder #(.width(32)) bitfinder_23 (.in(n23), .found(bitfinder_23_found));  // open: index
  BitFinder #(.width(32)) bitfinder_24 (.in(n24), .found(bitfinder_24_found));  // open: index
  BitFinder #(.width(32)) bitfinder_25 (.in(n25), .found(bitfinder_25_found));  // open: index
  BitFinder #(.width(32)) bitfinder_26 (.in(n26), .found(bitfinder_26_found));  // open: index
  BitFinder #(.width(32)) bitfinder_27 (.in(n27), .found(bitfinder_27_found));  // open: index
  BitFinder #(.width(32)) bitfinder_28 (.in(n28), .found(bitfinder_28_found));  // open: index
  BitFinder #(.width(32)) bitfinder_29 (.in(n29), .found(bitfinder_29_found));  // open: index
  BitFinder #(.width(32)) bitfinder_30 (.in(n30), .found(bitfinder_30_found));  // open: index
  BitFinder #(.width(32)) bitfinder_31 (.in(n31), .found(bitfinder_31_found));  // open: index
  BitFinder #(.width(32)) bitfinder_32 (.in(n32), .found(bitfinder_32_found));  // open: index
  Pull_Resistor pull_resistor_49 (.node(val17));
  assign val17 = bitfinder_17_found ? 4'b0010 : 4'bz;  // Controlled_Buffer controlled_buffer_49
  Pull_Resistor pull_resistor_50 (.node(val18));
  assign val18 = bitfinder_18_found ? 4'b0011 : 4'bz;  // Controlled_Buffer controlled_buffer_50
  Pull_Resistor pull_resistor_51 (.node(val19));
  assign val19 = bitfinder_19_found ? 4'b0100 : 4'bz;  // Controlled_Buffer controlled_buffer_51
  Pull_Resistor pull_resistor_52 (.node(val20));
  assign val20 = bitfinder_20_found ? 4'b0101 : 4'bz;  // Controlled_Buffer controlled_buffer_52
  Pull_Resistor pull_resistor_53 (.node(val21));
  assign val21 = bitfinder_21_found ? 4'b0110 : 4'bz;  // Controlled_Buffer controlled_buffer_53
  Pull_Resistor pull_resistor_54 (.node(val22));
  assign val22 = bitfinder_22_found ? 4'b0111 : 4'bz;  // Controlled_Buffer controlled_buffer_54
  Pull_Resistor pull_resistor_55 (.node(val23));
  assign val23 = bitfinder_23_found ? 4'b1000 : 4'bz;  // Controlled_Buffer controlled_buffer_55
  Pull_Resistor pull_resistor_56 (.node(val24));
  assign val24 = bitfinder_24_found ? 4'b1001 : 4'bz;  // Controlled_Buffer controlled_buffer_56
  Pull_Resistor pull_resistor_57 (.node(val25));
  assign val25 = bitfinder_25_found ? 4'b0010 : 4'bz;  // Controlled_Buffer controlled_buffer_57
  Pull_Resistor pull_resistor_58 (.node(val26));
  assign val26 = bitfinder_26_found ? 4'b0011 : 4'bz;  // Controlled_Buffer controlled_buffer_58
  Pull_Resistor pull_resistor_59 (.node(val27));
  assign val27 = bitfinder_27_found ? 4'b0100 : 4'bz;  // Controlled_Buffer controlled_buffer_59
  Pull_Resistor pull_resistor_60 (.node(val28));
  assign val28 = bitfinder_28_found ? 4'b0101 : 4'bz;  // Controlled_Buffer controlled_buffer_60
  Pull_Resistor pull_resistor_61 (.node(val29));
  assign val29 = bitfinder_29_found ? 4'b0110 : 4'bz;  // Controlled_Buffer controlled_buffer_61
  Pull_Resistor pull_resistor_62 (.node(val30));
  assign val30 = bitfinder_30_found ? 4'b0111 : 4'bz;  // Controlled_Buffer controlled_buffer_62
  Pull_Resistor pull_resistor_63 (.node(val31));
  assign val31 = bitfinder_31_found ? 4'b1000 : 4'bz;  // Controlled_Buffer controlled_buffer_63
  Pull_Resistor pull_resistor_64 (.node(val32));
  assign val32 = bitfinder_32_found ? 4'b1001 : 4'bz;  // Controlled_Buffer controlled_buffer_64
  assign nor_1_out = ~(n1 | n2 | n3 | n4 | n5 | n6 | n7 | n8 | n9 | n10 | n11 | n12 | n13 | n14 | n15 | n16 | n17 | n18 | n19 | n20 | n21 | n22 | n23 | n24 | n25 | n26 | n27 | n28 | n29 | n30 | n31 | n32);  // NOR_Gate nor_1, 32 bits wide
  assign card = val1 | val2 | val3 | val4 | val5 | val6 | val7 | val8 | val9 | val10 | val11 | val12 | val13 | val14 | val15 | val16 | val17 | val18 | val19 | val20 | val21 | val22 | val23 | val24 | val25 | val26 | val27 | val28 | val29 | val30 | val31 | val32;  // OR_Gate or_1, 4 bits wide
  assign final_colod = nor_1_out & colods;  // AND_Gate and_33, 32 bits wide
endmodule

module generator (
  input  clock,
  input  reset,
  output [7:0] address,
  output [7:0] data,
  output l_d,
  output clock_gen,
  output gen_done
);

  wire bitfinder_1_found, comparator_1_eq, comparator_2_eq, comparator_3_eq, comparator_4_eq,
       comparator_5_eq, comparator_6_eq, comparator_7_eq, comparator_8_gt, comparator_9_eq, comparator_10_eq,
       comparator_12_eq, eq_0, gen_done_t, not_1_out, not_2_out, not_3_out, not_4_out, not_5_out, or_1_out,
       or_2_out, tact;
  wire [3:0] configuration_1_card;
  wire [4:0] adder_1_out, multiplexer_2_out, register_1_q;
  wire [7:0] addr, counter_1_q, counter_2_q;
  wire [7:7] controlled_buffer_2_out;
  wire [31:0] configuration_1_final_colod, multiplexer_3_out, multiplexer_4_out, pull_resistor_2_node;

  Multiplexer #(.select(5), .width(8), .disabled(0), .enable("false")) multiplexer_1 (
    .in0(8'h91), .in1(8'h92), .in2(8'h9a), .in3(8'h9b), .in4(8'h9c), .in5(8'ha4), .in6(8'ha5), .in7(8'ha6),
    .in8(8'ha7), .in9(8'haf), .in10(8'hb0), .in11(8'hb1), .in12(8'hb2), .in13(8'hb3), .in14(8'hbb),
    .in15(8'hbc), .in16(8'hbd), .in17(8'hbe), .in18(8'hbf), .in19(8'hc8), .in20(8'hc9), .in21(8'hca),
    .in22(8'hcb), .in23(8'hcc), .in24(8'hcd), .in25(8'hd6), .in26(8'hd7), .in27(8'hd8), .in28(8'hd9),
    .in29(8'hda), .in30(8'hdb), .in31(8'hdc), .out(addr), .sel(register_1_q));
  Multiplexer #(.width(5), .enable("false")) multiplexer_2 (
    .in0({5{1'b0}}), .in1(adder_1_out), .out(multiplexer_2_out), .sel(comparator_8_gt));
  and and_1 (tact, clock, gen_done_t);
  Adder #(.width(5)) adder_1 (.a(register_1_q), .b(5'b00001), .out(adder_1_out));  // open: cin, cout
  not not_1 (not_1_out, eq_0);
  Counter counter_1 (.D({8{1'b0}}), .Q(counter_1_q), .clk(tact), .clr(reset));  // open: load, count, carry
  Comparator comparator_1 (.a(8'h92), .b(addr), .eq(comparator_1_eq));  // open: gt, lt
  Comparator comparator_2 (.a(8'h9c), .b(addr), .eq(comparator_2_eq));  // open: gt, lt
  Comparator comparator_3 (.a(8'ha7), .b(addr), .eq(comparator_3_eq));  // open: gt, lt
  Comparator comparator_4 (.a(8'hb3), .b(addr), .eq(comparator_4_eq));  // open: gt, lt
  Comparator comparator_5 (.a(8'hbf), .b(addr), .eq(comparator_5_eq));  // open: gt, lt
  Comparator comparator_6 (.a(8'hcd), .b(addr), .eq(comparator_6_eq));  // open: gt, lt
  Comparator comparator_7 (.a(8'hdc), .b(addr), .eq(comparator_7_eq));  // open: gt, lt
  Register #(.width(5)) register_1 (
    .D(multiplexer_2_out), .en(not_1_out), .Q(register_1_q), .clk(not_2_out), .clr(reset));
  not not_2 (not_2_out, tact);
  Comparator #(.mode("unsigned")) comparator_8 (.a(counter_1_q), .b({8{1'b0}}), .gt(comparator_8_gt));  // open: eq, lt
  or or_1 (or_1_out, gen_done_t, comparator_9_eq);
  or or_2 (or_2_out, comparator_1_eq, comparator_2_eq, comparator_3_eq, comparator_4_eq, comparator_5_eq, comparator_6_eq, comparator_7_eq);
  Multiplexer #(.width(32)) multiplexer_3 (
    .in0({32{1'b1}}), .in1(multiplexer_4_out), .out(multiplexer_3_out), .sel(not_3_out));  // open: en
  Counter counter_2 (.Q(counter_2_q), .clk(tact), .clr(reset));  // open: load, D, count, carry
  assign address = or_1_out ? addr : 8'bz;  // Controlled_Buffer controlled_buffer_1
  Comparator #(.mode("unsigned")) comparator_9 (.a(8'hdc), .b(addr), .eq(comparator_9_eq));  // open: gt, lt
  assign controlled_buffer_2_out[7] = or_2_out ? 1'b0 : 1'bz;  // Controlled_Buffer controlled_buffer_2
  Pull_Resistor #(.pull(1)) pull_resistor_1 (.node(controlled_buffer_2_out[7]));
  Pull_Resistor #(.pull(1)) pull_resistor_2 (.node(pull_resistor_2_node));
  assign pull_resistor_2_node = bitfinder_1_found ? multiplexer_3_out : 32'bz;  // Controlled_Buffer controlled_buffer_3
  Comparator #(.mode("unsigned")) comparator_10 (
    .a({8{1'b0}}), .b(counter_2_q), .eq(comparator_10_eq));  // open: gt, lt
  not not_3 (not_3_out, comparator_10_eq);
  BitFinder bitfinder_1 (.in(counter_2_q), .found(bitfinder_1_found));  // open: index
  configuration configuration_1 (
    .colods(pull_resistor_2_node), .clock(clock), .card(configuration_1_card),
    .final_colod(configuration_1_final_colod));
  Multiplexer #(.width(32), .enable("false")) multiplexer_4 (
    .in0(pull_resistor_2_node), .in1(configuration_1_final_colod), .out(multiplexer_4_out), .sel(not_4_out));
  not not_4 (not_4_out, clock);
  assign l_d = gen_done_t ? eq_0 : 1'bz;  // Controlled_Buffer controlled_buffer_4
  assign clock_gen = gen_done_t ? not_5_out : 1'bz;  // Controlled_Buffer controlled_buffer_5
  not not_5 (not_5_out, clock);
  Hex_Digit_Display hex_digit_display_1 (.value(configuration_1_card));  // open: dp
  assign data = gen_done_t ? {controlled_buffer_2_out[7], 3'b100, configuration_1_card} : 8'bz;  // Controlled_Buffer controlled_buffer_6
  Comparator #(.width(4)) comparator_11 (.a(4'b0000), .b(configuration_1_card), .eq(eq_0));  // open: gt, lt
  Comparator #(.width(32)) comparator_12 (
    .a({32{1'b0}}), .b(multiplexer_4_out), .eq(comparator_12_eq));  // open: gt, lt
  not not_6 (gen_done, gen_done_t);
  not not_7 (gen_done_t, comparator_12_eq);

  // Notes on the sheet:
  //   1 colon
  //   2 colon
  //   3 colon
  //   4 colon
  //   5 colon
  //   6 colon
  //   7 colon
  //   opened
  //   sentinels
  //   Chooses random card from colod
endmodule

module write_sentinels (
  input  clock,
  input  reset,
  output [7:0] address,
  output [7:0] data,
  output l_d,
  output clock_gen,
  output sent_writing_done
);

  wire comparator_1_gt, gen_done, not_1_out, not_2_out, tact;
  wire [2:0] adder_1_out, multiplexer_2_out, register_1_q;
  wire [7:0] addr, counter_1_q;

  Multiplexer #(.select(3), .width(8), .disabled(0), .enable("false")) multiplexer_1 (
    .in0(8'h90), .in1(8'h99), .in2(8'ha3), .in3(8'hae), .in4(8'hba), .in5(8'hc7), .in6(8'hd5),
    .in7({8{1'b1}}), .out(addr), .sel(register_1_q));
  Multiplexer #(.width(3), .enable("false")) multiplexer_2 (
    .in0(3'b000), .in1(adder_1_out), .out(multiplexer_2_out), .sel(comparator_1_gt));
  Counter counter_1 (.D({8{1'b0}}), .Q(counter_1_q), .clk(tact), .clr(reset));  // open: load, count, carry
  assign address = gen_done ? addr : 8'bz;  // Controlled_Buffer controlled_buffer_1
  Adder #(.width(3)) adder_1 (.a(register_1_q), .b(3'b001), .out(adder_1_out));  // open: cin, cout
  Register #(.width(3)) register_1 (
    .D(multiplexer_2_out), .en(gen_done), .Q(register_1_q), .clk(not_1_out), .clr(reset));
  not not_1 (not_1_out, tact);
  Comparator #(.mode("unsigned")) comparator_1 (.a(counter_1_q), .b({8{1'b0}}), .gt(comparator_1_gt));  // open: eq, lt
  assign l_d = gen_done ? 1'b0 : 1'bz;  // Controlled_Buffer controlled_buffer_2
  assign clock_gen = gen_done ? not_2_out : 1'bz;  // Controlled_Buffer controlled_buffer_3
  not not_2 (not_2_out, clock);
  assign data = gen_done ? 8'ha : 8'bz;  // Controlled_Buffer controlled_buffer_4
  Comparator #(.mode("unsigned")) comparator_2 (.a({8{1'b1}}), .b(addr), .eq(sent_writing_done));  // open: gt, lt
  and and_1 (tact, clock, gen_done);
  not not_3 (gen_done, sent_writing_done);

  // Notes on the sheet:
  //   opened
  //   sentinels
endmodule

module card_replace (
  input  [2:0] colod_number,
  input  [7:0] cur_command,
  output [7:0] updated_program,
  output move_done_updated
);

  wire _1st_done, _2st_done, and_1_out, and_2_out, and_3_out, and_4_out, and_5_out, and_6_out, and_7_out,
       and_8_out, colod_isnt_0, comparator_1_eq, not_equal, or_3_out, or_4_out;

  not not_1 (colod_isnt_0, comparator_1_eq);
  Comparator #(.width(3), .mode("unsigned")) comparator_1 (
    .a(colod_number), .b(3'b000), .eq(comparator_1_eq));  // open: gt, lt
  Comparator #(.width(3), .mode("unsigned")) comparator_2 (
    .a(colod_number), .b(cur_command[2:0]), .eq(not_equal));  // open: gt, lt
  or or_1 (_1st_done, cur_command[0], cur_command[1], cur_command[2], cur_command[3]);
  or or_2 (_2st_done, cur_command[4], cur_command[5], cur_command[6], cur_command[7]);
  and and_1 (and_1_out, _1st_done, _2st_done);
  or or_3 (or_3_out, updated_program[0], updated_program[1], updated_program[2], updated_program[3]);
  and and_2 (and_2_out, or_3_out, or_4_out);
  or or_4 (or_4_out, updated_program[4], updated_program[5], updated_program[6], updated_program[7]);
  or or_5 (move_done_updated, and_1_out, and_2_out);
  and and_3 (and_3_out, _1st_done, colod_isnt_0, _2st_done, ~not_equal);  // AND_Gate
  and and_4 (and_4_out, _1st_done, ~colod_isnt_0, _2st_done, ~not_equal);  // AND_Gate
  and and_5 (and_5_out, _1st_done, colod_isnt_0, ~_2st_done, ~not_equal);  // AND_Gate
  and and_6 (and_6_out, ~_1st_done, colod_isnt_0, ~_2st_done, ~not_equal);  // AND_Gate
  and and_7 (and_7_out, _1st_done, ~colod_isnt_0, ~_2st_done, ~not_equal);  // AND_Gate
  and and_8 (and_8_out, ~_1st_done, ~colod_isnt_0, ~_2st_done, ~not_equal);  // AND_Gate
  assign updated_program = and_3_out ? cur_command : 8'bz;  // Controlled_Buffer controlled_buffer_1
  assign updated_program = and_4_out ? cur_command : 8'bz;  // Controlled_Buffer controlled_buffer_2
  assign updated_program = and_5_out ? {1'b0, colod_number, cur_command[3:0]} : 8'bz;  // Controlled_Buffer controlled_buffer_3
  assign updated_program = and_6_out ? {cur_command[7:4], 1'b0, colod_number} : 8'bz;  // Controlled_Buffer controlled_buffer_4
  assign updated_program = and_7_out ? cur_command : 8'bz;  // Controlled_Buffer controlled_buffer_5
  assign updated_program = and_8_out ? cur_command : 8'bz;  // Controlled_Buffer controlled_buffer_6
  assign updated_program = not_equal ? cur_command : 8'bz;  // Controlled_Buffer controlled_buffer_7

  // Other names for the same wires on the sheet: c[2:0] = colod_number;
  //   case1 (some bits) = {cur_command[7:4], colod_number}; case2[6:0] = {colod_number, cur_command[3:0]};
  //   case3[7:0] = cur_command; command[7:0] = cur_command; res[7:0] = updated_program
endmodule

module print_cards (
  input  clock,
  input  move_done,
  output [7:0] adr,
  output print_done,
  output print
);

  wire pull_resistor_1_node;
  wire [7:0] adr_t;

  Counter counter_1 (.Q(adr_t), .clk(pull_resistor_1_node), .clr(move_done));  // open: load, D, count, carry
  Pull_Resistor pull_resistor_1 (.node(pull_resistor_1_node));
  assign pull_resistor_1_node = print ? clock : 1'bz;  // Controlled_Buffer controlled_buffer_1
  Comparator comparator_1 (.a(adr_t), .b(8'h4d), .lt(print));  // open: gt, eq
  ROM rom_1 (.addr(adr_t), .data(adr));  // open: sel
  Comparator comparator_2 (.a(adr), .b(8'he4), .eq(print_done));  // open: gt, lt

  // Notes on the sheet:
  //   sentinels
  //   cards
  //   contents of rom_1 (hex, n*v repeats v):
  //   91 92 93 94 95 96 97 98 9a 9b 9c 9d 9e 9f a0 a1 a2 a4 a5 a6 a7 a8 a9 aa ab ac ad af b0 b1 b2 b3 b4
  //   b5 b6 b7 b8 b9 bb bc bd be bf c0 c1 c2 c3 c4 c5 c6 c8 c9 ca cb cc cd ce cf d0 d1 d2 d3 d4 d6 d7 d8
  //   d9 da db dc dd de df e0 e1 e2 e3 e4
endmodule
