// Logisim project 2_clean.circ as structural Verilog: 10 circuits, main circuit main
module main (
);

  wire _1colod, _2colod, _3colod, _4colod, _5colod, _6colod, _7colod, _9a_e, _9c_e, _9d_e, _9e_e, _9f_e,
       _91_e, _92_e, _93_e, _94_e, _95_e, _96_e, _97_e, _98_e, _99_e, a0_e, a1_e, a2_e, a3_e, a4_e, a5_e,
       a6_e, a8_e, a9_e, aa_e, ab_e, ac_e, ad_e, ae_e, af_e, and_1_out, and_2_out, and_3_out, and_4_out,
       and_9_out, b0_e, b1_e, b2_e, b3_e, b5_e, b6_e, b7_e, b8_e, b9_e, ba_e, bb_e, bc_e, bd_e, be_e, bf_e,
       c0_e, c1_e, c3_e, c4_e, c5_e, c6_e, c7_e, c8_e, c9_e, ca_e, cancel_com, cb_e, cc_e, cd_e,
       cdm_8_mark5_1_p3, cdm_8_mark5_1_p4, cdm_8_mark5_1_p6, cdm_8_mark5_1_p7, cdm_8_mark5_1_p9,
       cdm_8_mark5_1_p10, ce_e, cf_e, Clock, code, com_enable, command_ld, d1_e, d2_e, d3_e, d4_e, d5_e,
       d6_e, d7_e, d8_e, d9_e, d_ff_1_q, da_e, data, db_e, dc_e, dd_e, de_e, disp_ready, drag_in_pr, e0_e,
       e1_e, e2_e, e3_e, e4_e, e5_e, e6_e, e7_e, e8_e, e9_e, ea_e, eb_e, ec_e, ed_e, ee_e, ef_e, f4_e,
       gen_done, gen_ld, IO_out_in_prime, IO_sel, memory, new_turn, not_1_out, not_2_out, not_3_out,
       not_4_out, not_5_out, not_6_out, not_7_out, not_8_out, ofs_done, ofs_ld, or_4_out, print_r, print_sel,
       RAM_r_wr_prime, RAM_sel, read_write, reset, run_com, run_command, run_prog, s_r_ff_2_qn, sent_done,
       sent_ld, start_game, wr_com, wr_enable, wr_enable_prime, zeroing;
  wire [3:0] _9a, _9c, _9d, _9e, _9f, _91, _92, _93, _94, _95, _96, _97, _98, _99, a0, a1, a2, a3, a4, a5,
       a6, a8, a9, aa, ab, ac, ad, ae, af, b0, b1, b2, b3, b5, b6, b7, b8, b9, ba, bb, bc, bd, be, bf, c0,
       c1, c3, c4, c5, c6, c7, c8, c9, ca, cb, cc, cd, ce, cf, com_value, d1, d2, d3, d4, d5, d6, d7, d8, d9,
       da, db, dc, dd, de, e0, e1, e2, e3, e4, e5, e6, e7, e8, e9, ea, eb, ec, ed, ee, f4, value;
  wire [4:0] multiplexer_4_out, multiplexer_5_out, multiplexer_6_out, multiplexer_7_out, multiplexer_8_out,
       multiplexer_9_out, multiplexer_10_out, multiplexer_11_out, multiplexer_12_out, multiplexer_13_out,
       multiplexer_14_out, multiplexer_15_out, multiplexer_16_out, multiplexer_17_out;
  wire [6:0] bit_extender_1_out;
  wire [7:0] addr, card_value, cdm_8_mark5_1_p14, cdm_8_mark5_1_p15, command_address, command_data,
       current_command, data_base, pc, print_address, RAM_address, subtractor_1_out;

  _128_decoder u_128_decoder_1 (
    .select(bit_extender_1_out), ._1(_91_e), ._65(d1_e), ._2(_92_e), ._66(d2_e), ._3(_93_e), ._67(d3_e),
    ._4(_94_e), ._68(d4_e), ._5(_95_e), ._69(d5_e), ._6(_96_e), ._70(d6_e), ._7(_97_e), ._71(d7_e),
    ._8(_98_e), ._72(d8_e), ._9(_99_e), ._73(d9_e), ._10(_9a_e), ._74(da_e), ._75(db_e), ._12(_9c_e),
    ._76(dc_e), ._13(_9d_e), ._77(dd_e), ._14(_9e_e), ._78(de_e), ._15(_9f_e), ._16(a0_e), ._80(e0_e),
    ._17(a1_e), ._81(e1_e), ._18(a2_e), ._82(e2_e), ._19(a3_e), ._83(e3_e), ._20(a4_e), ._84(e4_e),
    ._21(a5_e), ._85(e5_e), ._22(a6_e), ._86(e6_e), ._87(e7_e), ._24(a8_e), ._88(e8_e), ._25(a9_e),
    ._89(e9_e), ._26(aa_e), ._90(ea_e), ._27(ab_e), ._91(eb_e), ._28(ac_e), ._92(ec_e), ._29(ad_e),
    ._93(ed_e), ._30(ae_e), ._94(ee_e), ._31(af_e), ._95(ef_e), ._32(b0_e), ._33(b1_e), ._34(b2_e),
    ._35(b3_e), ._100(f4_e), ._37(b5_e), ._38(b6_e), ._39(b7_e), ._40(b8_e), ._41(b9_e), ._42(ba_e),
    ._43(bb_e), ._44(bc_e), ._45(bd_e), ._46(be_e), ._47(bf_e), ._48(c0_e), ._49(c1_e), ._51(c3_e),
    ._52(c4_e), ._53(c5_e), ._54(c6_e), ._55(c7_e), ._56(c8_e), ._57(c9_e), ._58(ca_e), ._59(cb_e),
    ._60(cc_e), ._61(cd_e), ._62(ce_e), ._63(cf_e));  // open: _0, _64, _11, _79, _23, _96, _97, _98, _99, _36, _101, _102, _103, _104, _105, _106, _107, _108, _109, _110, _111, _112, _113, _50, _114, _115, _116, _117, _118, _119, _120, _121, _122, _123, _124, _125, _126, _127
  Subtractor subtractor_1 (.a(print_address), .b(8'h90), .out(subtractor_1_out));  // open: bin, bout
  Bit_Extender #(.out_width(7)) bit_extender_1 (.in(subtractor_1_out), .out(bit_extender_1_out));
  Pull_Resistor pull_resistor_1 (.node(bit_extender_1_out));
  D_Flip_Flop d_ff_1 (.Q(d_ff_1_q), .preset(run_prog), .reset(and_3_out));  // open: clk, D, Qn, en
  S_R_Flip_Flop s_r_ff_1 (.Qn(drag_in_pr), .preset(new_turn), .reset(run_prog));  // open: S, clk, R, Q, en
  and and_1 (and_1_out, ~IO_sel, read_write);  // AND_Gate
  assign data_base = and_1_out ? card_value : 8'bz;  // Controlled_Buffer controlled_buffer_1
  assign card_value = and_2_out ? data_base : 8'bz;  // Controlled_Buffer controlled_buffer_2
  and and_2 (and_2_out, ~IO_sel, ~read_write);  // AND_Gate
  buf buffer_1 (IO_sel, gen_ld);
  buf buffer_2 (IO_out_in_prime, gen_ld);
  buf buffer_3 (IO_sel, sent_ld);
  buf buffer_4 (IO_out_in_prime, sent_ld);
  buf buffer_5 (IO_sel, print_sel);
  buf buffer_6 (IO_out_in_prime, print_r);
  buf buffer_7 (IO_sel, command_ld);
  buf buffer_8 (IO_out_in_prime, command_ld);
  buf buffer_9 (IO_sel, ofs_ld);
  buf buffer_10 (IO_out_in_prime, ofs_ld);
  // NOT_Gate not_1 has open pins: in=open, out=not_1_out
  and and_3 (and_3_out, not_1_out, not_2_out);
  not not_2 (not_2_out, not_1_out);
  assign command_address = print_address;  // Buffer buffer_11, 8 bits wide
  Register #(.width(4), .trigger("falling")) register_1 (.D(value), .en(_91_e), .Q(_91), .clk(Clock));  // open: clr
  Register #(.width(4), .trigger("falling")) register_2 (.D(value), .en(_92_e), .Q(_92), .clk(Clock));  // open: clr
  Register #(.width(4), .trigger("falling")) register_3 (.D(value), .en(_93_e), .Q(_93), .clk(Clock));  // open: clr
  Register #(.width(4), .trigger("falling")) register_4 (.D(value), .en(_94_e), .Q(_94), .clk(Clock));  // open: clr
  Register #(.width(4), .trigger("falling")) register_5 (.D(value), .en(_95_e), .Q(_95), .clk(Clock));  // open: clr
  Register #(.width(4), .trigger("falling")) register_6 (.D(value), .en(_96_e), .Q(_96), .clk(Clock));  // open: clr
  Register #(.width(4), .trigger("falling")) register_7 (.D(value), .en(_97_e), .Q(_97), .clk(Clock));  // open: clr
  Register #(.width(4), .trigger("falling")) register_8 (.D(value), .en(_98_e), .Q(_98), .clk(Clock));  // open: clr
  Register #(.width(4), .trigger("falling")) register_9 (.D(value), .en(_99_e), .Q(_99), .clk(Clock));  // open: clr
  Register #(.width(4), .trigger("falling")) register_10 (.D(value), .en(_9a_e), .Q(_9a), .clk(Clock));  // open: clr
  Register #(.width(4), .trigger("falling")) register_11 (.D(value), .en(f4_e), .Q(f4), .clk(Clock));  // open: clr
  // Probe on cdm_8_mark5_1_p4
  // Probe on cdm_8_mark5_1_p6
  // Probe on cdm_8_mark5_1_p7
  // Probe on cdm_8_mark5_1_p3
  Clock clock_1 (.out(Clock));
  not not_3 (not_3_out, IO_out_in_prime);
  Multiplexer #(.width(4), .enable("false")) multiplexer_1 (
    .in0(card_value[3:0]), .in1(4'b1100), .out(value), .sel(card_value[7]));
  // Probe on cdm_8_mark5_1_p9
  // CdM_8_mark5 cdm_8_mark5_1: pin names not known; wires that end beside it: d_ff_1_q, 3'b000, cdm_8_mark5_1_p3, cdm_8_mark5_1_p4, Clock, cdm_8_mark5_1_p6, cdm_8_mark5_1_p7, pc, cdm_8_mark5_1_p9, cdm_8_mark5_1_p10, memory, read_write, addr, cdm_8_mark5_1_p14, cdm_8_mark5_1_p15
  and and_4 (and_4_out, ~pc[0], ~pc[1], pc[2], pc[3], ~pc[4], ~pc[5], ~pc[6], ~pc[7]);  // AND_Gate
  or or_1 (RAM_sel, IO_sel, data);
  Multiplexer #(.enable("false")) multiplexer_2 (.in0(read_write), .in1(not_3_out), .out(RAM_r_wr_prime), .sel(IO_sel));
  Multiplexer #(.width(8), .enable("false")) multiplexer_3 (
    .in0(addr), .in1(command_address), .out(RAM_address), .sel(IO_sel));
  assign card_value = IO_sel ? command_data : 8'bz;  // Controlled_Buffer controlled_buffer_3
  Decoder #(.disabled(0)) decoder_1 (.out0(code), .out1(data), .sel(cdm_8_mark5_1_p10), .en(memory));
  assign data_base = not_4_out ? cdm_8_mark5_1_p14 : 8'bz;  // Controlled_Buffer controlled_buffer_4
  not not_4 (not_4_out, read_write);
  assign cdm_8_mark5_1_p15 = read_write ? data_base : 8'bz;  // Controlled_Buffer controlled_buffer_5
  and and_5 (new_turn, and_4_out, not_5_out);
  not not_5 (not_5_out, and_4_out);
  Register #(.width(4), .trigger("falling")) register_12 (.D(value), .en(_9c_e), .Q(_9c), .clk(Clock));  // open: clr
  Register #(.width(4), .trigger("falling")) register_13 (.D(value), .en(_9d_e), .Q(_9d), .clk(Clock));  // open: clr
  Register #(.width(4), .trigger("falling")) register_14 (.D(value), .en(_9e_e), .Q(_9e), .clk(Clock));  // open: clr
  Register #(.width(4), .trigger("falling")) register_15 (.D(value), .en(_9f_e), .Q(_9f), .clk(Clock));  // open: clr
  Register #(.width(4), .trigger("falling")) register_16 (.D(value), .en(a0_e), .Q(a0), .clk(Clock));  // open: clr
  Register #(.width(4), .trigger("falling")) register_17 (.D(value), .en(a1_e), .Q(a1), .clk(Clock));  // open: clr
  Register #(.width(4), .trigger("falling")) register_18 (.D(value), .en(a2_e), .Q(a2), .clk(Clock));  // open: clr
  Register #(.width(4), .trigger("falling")) register_19 (.D(value), .en(a3_e), .Q(a3), .clk(Clock));  // open: clr
  Register #(.width(4), .trigger("falling")) register_20 (.D(value), .en(a4_e), .Q(a4), .clk(Clock));  // open: clr
  Register #(.width(4), .trigger("falling")) register_21 (.D(value), .en(a5_e), .Q(a5), .clk(Clock));  // open: clr
  Register #(.width(4), .trigger("falling")) register_22 (.D(value), .en(a6_e), .Q(a6), .clk(Clock));  // open: clr
  // Probe on RAM_address
  Pull_Resistor pull_resistor_2 (.node(IO_sel));
  Register #(.width(4), .trigger("falling")) register_23 (.D(value), .en(a8_e), .Q(a8), .clk(Clock));  // open: clr
  Register #(.width(4), .trigger("falling")) register_24 (.D(value), .en(a9_e), .Q(a9), .clk(Clock));  // open: clr
  Register #(.width(4), .trigger("falling")) register_25 (.D(value), .en(aa_e), .Q(aa), .clk(Clock));  // open: clr
  Register #(.width(4), .trigger("falling")) register_26 (.D(value), .en(ab_e), .Q(ab), .clk(Clock));  // open: clr
  Register #(.width(4), .trigger("falling")) register_27 (.D(value), .en(ac_e), .Q(ac), .clk(Clock));  // open: clr
  Register #(.width(4), .trigger("falling")) register_28 (.D(value), .en(ad_e), .Q(ad), .clk(Clock));  // open: clr
  Register #(.width(4), .trigger("falling")) register_29 (.D(value), .en(ae_e), .Q(ae), .clk(Clock));  // open: clr
  Register #(.width(4), .trigger("falling")) register_30 (.D(value), .en(af_e), .Q(af), .clk(Clock));  // open: clr
  Register #(.width(4), .trigger("falling")) register_31 (.D(value), .en(b0_e), .Q(b0), .clk(Clock));  // open: clr
  Register #(.width(4), .trigger("falling")) register_32 (.D(value), .en(b1_e), .Q(b1), .clk(Clock));  // open: clr
  Register #(.width(4), .trigger("falling")) register_33 (.D(value), .en(b2_e), .Q(b2), .clk(Clock));  // open: clr
  Register #(.width(4), .trigger("falling")) register_34 (.D(value), .en(b3_e), .Q(b3), .clk(Clock));  // open: clr
  // Probe on addr
  RAM ram_1 (.addr(RAM_address), .data(card_value), .sel(RAM_sel), .clk(Clock), .ld(RAM_r_wr_prime), .clr(reset));
  // Probe on card_value
  Register #(.width(4), .trigger("falling")) register_35 (.D(value), .en(b5_e), .Q(b5), .clk(Clock));  // open: clr
  Register #(.width(4), .trigger("falling")) register_36 (.D(value), .en(b6_e), .Q(b6), .clk(Clock));  // open: clr
  Register #(.width(4), .trigger("falling")) register_37 (.D(value), .en(b7_e), .Q(b7), .clk(Clock));  // open: clr
  Register #(.width(4), .trigger("falling")) register_38 (.D(value), .en(b8_e), .Q(b8), .clk(Clock));  // open: clr
  Register #(.width(4), .trigger("falling")) register_39 (.D(value), .en(b9_e), .Q(b9), .clk(Clock));  // open: clr
  Register #(.width(4), .trigger("falling")) register_40 (.D(value), .en(ba_e), .Q(ba), .clk(Clock));  // open: clr
  Register #(.width(4), .trigger("falling")) register_41 (.D(value), .en(bb_e), .Q(bb), .clk(Clock));  // open: clr
  Register #(.width(4), .trigger("falling")) register_42 (.D(value), .en(bc_e), .Q(bc), .clk(Clock));  // open: clr
  Register #(.width(4), .trigger("falling")) register_43 (.D(value), .en(bd_e), .Q(bd), .clk(Clock));  // open: clr
  Register #(.width(4), .trigger("falling")) register_44 (.D(value), .en(be_e), .Q(be), .clk(Clock));  // open: clr
  Register #(.width(4), .trigger("falling")) register_45 (.D(value), .en(bf_e), .Q(bf), .clk(Clock));  // open: clr
  Register #(.width(4), .trigger("falling")) register_46 (.D(value), .en(c0_e), .Q(c0), .clk(Clock));  // open: clr
  Register #(.width(4), .trigger("falling")) register_47 (.D(value), .en(c1_e), .Q(c1), .clk(Clock));  // open: clr
  // Probe on data_base
  ROM rom_1 (.addr(addr), .data(data_base), .sel(code));
  and and_6 (reset, ~drag_in_pr, disp_ready, start_game);  // AND_Gate
  and and_7 (run_com, ~drag_in_pr, disp_ready, run_command);  // AND_Gate
  Register #(.width(4), .trigger("falling")) register_48 (.D(value), .en(c3_e), .Q(c3), .clk(Clock));  // open: clr
  Register #(.width(4), .trigger("falling")) register_49 (.D(value), .en(c4_e), .Q(c4), .clk(Clock));  // open: clr
  Register #(.width(4), .trigger("falling")) register_50 (.D(value), .en(c5_e), .Q(c5), .clk(Clock));  // open: clr
  Register #(.width(4), .trigger("falling")) register_51 (.D(value), .en(c6_e), .Q(c6), .clk(Clock));  // open: clr
  Register #(.width(4), .trigger("falling")) register_52 (.D(value), .en(c7_e), .Q(c7), .clk(Clock));  // open: clr
  Register #(.width(4), .trigger("falling")) register_53 (.D(value), .en(c8_e), .Q(c8), .clk(Clock));  // open: clr
  Register #(.width(4), .trigger("falling")) register_54 (.D(value), .en(c9_e), .Q(c9), .clk(Clock));  // open: clr
  Register #(.width(4), .trigger("falling")) register_55 (.D(value), .en(ca_e), .Q(ca), .clk(Clock));  // open: clr
  Register #(.width(4), .trigger("falling")) register_56 (.D(value), .en(cb_e), .Q(cb), .clk(Clock));  // open: clr
  Register #(.width(4), .trigger("falling")) register_57 (.D(value), .en(cc_e), .Q(cc), .clk(Clock));  // open: clr
  Register #(.width(4), .trigger("falling")) register_58 (.D(value), .en(cd_e), .Q(cd), .clk(Clock));  // open: clr
  Register #(.width(4), .trigger("falling")) register_59 (.D(value), .en(ce_e), .Q(ce), .clk(Clock));  // open: clr
  Register #(.width(4), .trigger("falling")) register_60 (.D(value), .en(cf_e), .Q(cf), .clk(Clock));  // open: clr
  Hex_Digit_Display hex_digit_display_1 (.value(current_command[7:4]));  // open: dp
  Button button_1 (.out(start_game));
  Button button_2 (.out(run_command));
  Button button_3 (.out(cancel_com));
  Hex_Digit_Display hex_digit_display_2 (.value(current_command[3:0]));  // open: dp
  Register #(.width(4), .trigger("falling")) register_61 (.D(value), .en(d1_e), .Q(d1), .clk(Clock));  // open: clr
  Register #(.width(4), .trigger("falling")) register_62 (.D(value), .en(d2_e), .Q(d2), .clk(Clock));  // open: clr
  Register #(.width(4), .trigger("falling")) register_63 (.D(value), .en(d3_e), .Q(d3), .clk(Clock));  // open: clr
  Register #(.width(4), .trigger("falling")) register_64 (.D(value), .en(d4_e), .Q(d4), .clk(Clock));  // open: clr
  Register #(.width(4), .trigger("falling")) register_65 (.D(value), .en(d5_e), .Q(d5), .clk(Clock));  // open: clr
  Register #(.width(4), .trigger("falling")) register_66 (.D(value), .en(d6_e), .Q(d6), .clk(Clock));  // open: clr
  Register #(.width(4), .trigger("falling")) register_67 (.D(value), .en(d7_e), .Q(d7), .clk(Clock));  // open: clr
  Register #(.width(4), .trigger("falling")) register_68 (.D(value), .en(d8_e), .Q(d8), .clk(Clock));  // open: clr
  Register #(.width(4), .trigger("falling")) register_69 (.D(value), .en(d9_e), .Q(d9), .clk(Clock));  // open: clr
  Register #(.width(4), .trigger("falling")) register_70 (.D(value), .en(da_e), .Q(da), .clk(Clock));  // open: clr
  Register #(.width(4), .trigger("falling")) register_71 (.D(value), .en(db_e), .Q(db), .clk(Clock));  // open: clr
  Register #(.width(4), .trigger("falling")) register_72 (.D(value), .en(dc_e), .Q(dc), .clk(Clock));  // open: clr
  Register #(.width(4), .trigger("falling")) register_73 (.D(value), .en(dd_e), .Q(dd), .clk(Clock));  // open: clr
  Register #(.width(4), .trigger("falling")) register_74 (.D(value), .en(de_e), .Q(de), .clk(Clock));  // open: clr
  not not_6 (not_6_out, not_6_out);
  Button button_4 (.out(_1colod));
  Hex_Digit_Display hex_digit_display_3 (.value(_91));  // open: dp
  Hex_Digit_Display hex_digit_display_4 (.value(_92));  // open: dp
  Hex_Digit_Display hex_digit_display_5 (.value(_93));  // open: dp
  Hex_Digit_Display hex_digit_display_6 (.value(_94));  // open: dp
  Hex_Digit_Display hex_digit_display_7 (.value(_95));  // open: dp
  Hex_Digit_Display hex_digit_display_8 (.value(_96));  // open: dp
  Hex_Digit_Display hex_digit_display_9 (.value(_97));  // open: dp
  Hex_Digit_Display hex_digit_display_10 (.value(_98));  // open: dp
  Hex_Digit_Display hex_digit_display_11 (.value(_99));  // open: dp
  Hex_Digit_Display hex_digit_display_12 (.value(_9a));  // open: dp
  Register #(.width(4), .trigger("falling")) register_75 (.D(value), .en(e0_e), .Q(e0), .clk(Clock));  // open: clr
  Register #(.width(4), .trigger("falling")) register_76 (.D(value), .en(e1_e), .Q(e1), .clk(Clock));  // open: clr
  Register #(.width(4), .trigger("falling")) register_77 (.D(value), .en(e2_e), .Q(e2), .clk(Clock));  // open: clr
  Register #(.width(4), .trigger("falling")) register_78 (.D(value), .en(e3_e), .Q(e3), .clk(Clock));  // open: clr
  Register #(.width(4), .trigger("falling")) register_79 (.D(value), .en(e4_e), .Q(e4), .clk(Clock));  // open: clr
  Register #(.width(4), .trigger("falling")) register_80 (.D(value), .en(e5_e), .Q(e5), .clk(Clock));  // open: clr
  Register #(.width(4), .trigger("falling")) register_81 (.D(value), .en(e6_e), .Q(e6), .clk(Clock));  // open: clr
  Register #(.width(4), .trigger("falling")) register_82 (.D(value), .en(e7_e), .Q(e7), .clk(Clock));  // open: clr
  Register #(.width(4), .trigger("falling")) register_83 (.D(value), .en(e8_e), .Q(e8), .clk(Clock));  // open: clr
  Register #(.width(4), .trigger("falling")) register_84 (.D(value), .en(e9_e), .Q(e9), .clk(Clock));  // open: clr
  Register #(.width(4), .trigger("falling")) register_85 (.D(value), .en(ea_e), .Q(ea), .clk(Clock));  // open: clr
  Register #(.width(4), .trigger("falling")) register_86 (.D(value), .en(eb_e), .Q(eb), .clk(Clock));  // open: clr
  Register #(.width(4), .trigger("falling")) register_87 (.D(value), .en(ec_e), .Q(ec), .clk(Clock));  // open: clr
  Register #(.width(4), .trigger("falling")) register_88 (.D(value), .en(ed_e), .Q(ed), .clk(Clock));  // open: clr
  Register #(.width(4), .trigger("falling")) register_89 (.D(value), .en(ee_e), .Q(ee), .clk(Clock));  // open: clr
  Button button_5 (.out(_2colod));
  Hex_Digit_Display hex_digit_display_13 (.value(_9c));  // open: dp
  Hex_Digit_Display hex_digit_display_14 (.value(_9d));  // open: dp
  Hex_Digit_Display hex_digit_display_15 (.value(_9e));  // open: dp
  Hex_Digit_Display hex_digit_display_16 (.value(_9f));  // open: dp
  Hex_Digit_Display hex_digit_display_17 (.value(a0));  // open: dp
  Hex_Digit_Display hex_digit_display_18 (.value(a1));  // open: dp
  Hex_Digit_Display hex_digit_display_19 (.value(a2));  // open: dp
  Hex_Digit_Display hex_digit_display_20 (.value(a3));  // open: dp
  Hex_Digit_Display hex_digit_display_21 (.value(a4));  // open: dp
  Hex_Digit_Display hex_digit_display_22 (.value(a5));  // open: dp
  Hex_Digit_Display hex_digit_display_23 (.value(a6));  // open: dp
  Button button_6 (.out(_3colod));
  Hex_Digit_Display hex_digit_display_24 (.value(a8));  // open: dp
  Hex_Digit_Display hex_digit_display_25 (.value(a9));  // open: dp
  Hex_Digit_Display hex_digit_display_26 (.value(aa));  // open: dp
  Hex_Digit_Display hex_digit_display_27 (.value(ab));  // open: dp
  Hex_Digit_Display hex_digit_display_28 (.value(ac));  // open: dp
  Hex_Digit_Display hex_digit_display_29 (.value(ad));  // open: dp
  Hex_Digit_Display hex_digit_display_30 (.value(ae));  // open: dp
  Hex_Digit_Display hex_digit_display_31 (.value(af));  // open: dp
  Hex_Digit_Display hex_digit_display_32 (.value(b0));  // open: dp
  Hex_Digit_Display hex_digit_display_33 (.value(b1));  // open: dp
  Hex_Digit_Display hex_digit_display_34 (.value(b2));  // open: dp
  Hex_Digit_Display hex_digit_display_35 (.value(b3));  // open: dp
  assign com_value = _1colod ? 4'b0001 : 4'bz;  // Controlled_Buffer controlled_buffer_6
  assign com_value = _2colod ? 4'b0010 : 4'bz;  // Controlled_Buffer controlled_buffer_7
  assign com_value = _3colod ? 4'b0011 : 4'bz;  // Controlled_Buffer controlled_buffer_8
  assign com_value = _4colod ? 4'b0100 : 4'bz;  // Controlled_Buffer controlled_buffer_9
  assign com_value = _5colod ? 4'b0101 : 4'bz;  // Controlled_Buffer controlled_buffer_10
  assign com_value = _6colod ? 4'b0110 : 4'bz;  // Controlled_Buffer controlled_buffer_11
  assign com_value = _7colod ? 4'b0111 : 4'bz;  // Controlled_Buffer controlled_buffer_12
  Hex_Digit_Display hex_digit_display_36 (.value(b5));  // open: dp
  Hex_Digit_Display hex_digit_display_37 (.value(b6));  // open: dp
  Hex_Digit_Display hex_digit_display_38 (.value(b7));  // open: dp
  Hex_Digit_Display hex_digit_display_39 (.value(b8));  // open: dp
  Hex_Digit_Display hex_digit_display_40 (.value(b9));  // open: dp
  Hex_Digit_Display hex_digit_display_41 (.value(ba));  // open: dp
  Hex_Digit_Display hex_digit_display_42 (.value(bb));  // open: dp
  Hex_Digit_Display hex_digit_display_43 (.value(bc));  // open: dp
  Hex_Digit_Display hex_digit_display_44 (.value(bd));  // open: dp
  Hex_Digit_Display hex_digit_display_45 (.value(be));  // open: dp
  Hex_Digit_Display hex_digit_display_46 (.value(bf));  // open: dp
  Hex_Digit_Display hex_digit_display_47 (.value(c0));  // open: dp
  Hex_Digit_Display hex_digit_display_48 (.value(c1));  // open: dp
  Button button_7 (.out(_4colod));
  or or_2 (zeroing, reset, cancel_com, run_prog);
  or or_3 (wr_enable_prime, _1colod, _2colod, _3colod, _4colod, _5colod, _6colod, _7colod);
  Button button_8 (.out(_5colod));
  Hex_Digit_Display hex_digit_display_49 (.value(c3));  // open: dp
  Hex_Digit_Display hex_digit_display_50 (.value(c4));  // open: dp
  Hex_Digit_Display hex_digit_display_51 (.value(c5));  // open: dp
  Hex_Digit_Display hex_digit_display_52 (.value(c6));  // open: dp
  Hex_Digit_Display hex_digit_display_53 (.value(c7));  // open: dp
  Hex_Digit_Display hex_digit_display_54 (.value(c8));  // open: dp
  Hex_Digit_Display hex_digit_display_55 (.value(c9));  // open: dp
  Hex_Digit_Display hex_digit_display_56 (.value(ca));  // open: dp
  Hex_Digit_Display hex_digit_display_57 (.value(cb));  // open: dp
  Hex_Digit_Display hex_digit_display_58 (.value(cc));  // open: dp
  Hex_Digit_Display hex_digit_display_59 (.value(cd));  // open: dp
  Hex_Digit_Display hex_digit_display_60 (.value(ce));  // open: dp
  Hex_Digit_Display hex_digit_display_61 (.value(cf));  // open: dp
  my_replace my_replace_1 (
    .colod_number(com_value), .enable(wr_enable), .clock(Clock), .from_to(current_command), .reset(zeroing),
    .com_ready(com_enable));
  Button button_9 (.out(_6colod));
  Hex_Digit_Display hex_digit_display_62 (.value(d1));  // open: dp
  Hex_Digit_Display hex_digit_display_63 (.value(d2));  // open: dp
  Hex_Digit_Display hex_digit_display_64 (.value(d3));  // open: dp
  Hex_Digit_Display hex_digit_display_65 (.value(d4));  // open: dp
  Hex_Digit_Display hex_digit_display_66 (.value(d5));  // open: dp
  Hex_Digit_Display hex_digit_display_67 (.value(d6));  // open: dp
  Hex_Digit_Display hex_digit_display_68 (.value(d7));  // open: dp
  Hex_Digit_Display hex_digit_display_69 (.value(d8));  // open: dp
  Hex_Digit_Display hex_digit_display_70 (.value(d9));  // open: dp
  Hex_Digit_Display hex_digit_display_71 (.value(da));  // open: dp
  Hex_Digit_Display hex_digit_display_72 (.value(db));  // open: dp
  Hex_Digit_Display hex_digit_display_73 (.value(dc));  // open: dp
  Hex_Digit_Display hex_digit_display_74 (.value(dd));  // open: dp
  Hex_Digit_Display hex_digit_display_75 (.value(de));  // open: dp
  and and_8 (wr_enable, wr_enable_prime, not_7_out);
  not not_7 (not_7_out, wr_enable_prime);
  Button button_10 (.out(_7colod));
  Hex_Digit_Display hex_digit_display_76 (.value(e0));  // open: dp
  Hex_Digit_Display hex_digit_display_77 (.value(e1));  // open: dp
  Hex_Digit_Display hex_digit_display_78 (.value(e2));  // open: dp
  Hex_Digit_Display hex_digit_display_79 (.value(e3));  // open: dp
  Hex_Digit_Display hex_digit_display_80 (.value(e4));  // open: dp
  Hex_Digit_Display hex_digit_display_81 (.value(e5));  // open: dp
  Hex_Digit_Display hex_digit_display_82 (.value(e6));  // open: dp
  Hex_Digit_Display hex_digit_display_83 (.value(e7));  // open: dp
  Hex_Digit_Display hex_digit_display_84 (.value(e8));  // open: dp
  Hex_Digit_Display hex_digit_display_85 (.value(e9));  // open: dp
  Hex_Digit_Display hex_digit_display_86 (.value(ea));  // open: dp
  Hex_Digit_Display hex_digit_display_87 (.value(eb));  // open: dp
  Hex_Digit_Display hex_digit_display_88 (.value(ec));  // open: dp
  Hex_Digit_Display hex_digit_display_89 (.value(ed));  // open: dp
  Hex_Digit_Display hex_digit_display_90 (.value(ee));  // open: dp
  Hex_Digit_Display hex_digit_display_91 (.value(f4));  // open: dp
  write_sentinels write_sentinels_1 (
    .data(command_data), .clock(Clock), .reset(gen_done), .address(command_address), .sent_done(sent_done),
    .sent_ld(sent_ld));
  print_cards print_cards_1 (
    .clock(Clock), .adr(print_address), .print_sel(print_sel), .start(or_4_out), .print_r(print_r),
    .print_done(disp_ready));
  or or_4 (or_4_out, ofs_done, new_turn);
  assign command_data = wr_com ? current_command : 8'bz;  // Controlled_Buffer controlled_buffer_13
  assign command_address = wr_com ? 8'hf3 : 8'bz;  // Controlled_Buffer controlled_buffer_14
  assign command_ld = wr_com ? 1'b1 : 1'bz;  // Controlled_Buffer controlled_buffer_15
  Multiplexer #(.width(5), .enable("false")) multiplexer_4 (
    .in0({5{1'b0}}), .in1(5'b11110), .out(multiplexer_4_out), .sel(f4[2]));
  Multiplexer #(.width(5), .enable("false")) multiplexer_5 (
    .in0({5{1'b0}}), .in1(5'b00001), .out(multiplexer_5_out), .sel(f4[2]));
  Multiplexer #(.width(5), .enable("false")) multiplexer_6 (
    .in0({5{1'b0}}), .in1(5'b01110), .out(multiplexer_6_out), .sel(f4[2]));
  Multiplexer #(.width(5), .enable("false")) multiplexer_7 (
    .in0({5{1'b0}}), .in1(5'b00001), .out(multiplexer_7_out), .sel(f4[2]));
  Multiplexer #(.width(5), .enable("false")) multiplexer_8 (
    .in0({5{1'b0}}), .in1(5'b11110), .out(multiplexer_8_out), .sel(f4[2]));
  Multiplexer #(.width(5), .enable("false")) multiplexer_9 (
    .in0({5{1'b0}}), .in1({5{1'b0}}), .out(multiplexer_9_out), .sel(f4[2]));
  Multiplexer #(.width(5), .enable("false")) multiplexer_10 (
    .in0({5{1'b0}}), .in1(5'b10001), .out(multiplexer_10_out), .sel(f4[2]));
  Multiplexer #(.width(5), .enable("false")) multiplexer_11 (
    .in0({5{1'b0}}), .in1({5{1'b1}}), .out(multiplexer_11_out), .sel(f4[2]));
  Multiplexer #(.width(5), .enable("false")) multiplexer_12 (
    .in0({5{1'b0}}), .in1(5'b10001), .out(multiplexer_12_out), .sel(f4[2]));
  Multiplexer #(.width(5), .enable("false")) multiplexer_13 (
    .in0({5{1'b0}}), .in1({5{1'b0}}), .out(multiplexer_13_out), .sel(f4[2]));
  Multiplexer #(.width(5), .enable("false")) multiplexer_14 (
    .in0({5{1'b0}}), .in1({5{1'b1}}), .out(multiplexer_14_out), .sel(f4[2]));
  Multiplexer #(.width(5), .enable("false")) multiplexer_15 (
    .in0({5{1'b0}}), .in1(5'b01000), .out(multiplexer_15_out), .sel(f4[2]));
  Multiplexer #(.width(5), .enable("false")) multiplexer_16 (
    .in0({5{1'b0}}), .in1(5'b00100), .out(multiplexer_16_out), .sel(f4[2]));
  Multiplexer #(.width(5), .enable("false")) multiplexer_17 (
    .in0({5{1'b0}}), .in1({5{1'b1}}), .out(multiplexer_17_out), .sel(f4[2]));
  and and_9 (and_9_out, run_com, disp_ready, com_enable);
  DotMatrix #(.matrixcols(14), .matrixrows(5)) dotmatrix_1 (
    .col0(multiplexer_4_out), .col1(multiplexer_5_out), .col2(multiplexer_6_out), .col3(multiplexer_7_out),
    .col4(multiplexer_8_out), .col5(multiplexer_9_out), .col6(multiplexer_10_out), .col7(multiplexer_11_out),
    .col8(multiplexer_12_out), .col9(multiplexer_13_out), .col10(multiplexer_14_out),
    .col11(multiplexer_15_out), .col12(multiplexer_16_out), .col13(multiplexer_17_out));
  S_R_Flip_Flop s_r_ff_2 (
    .S(1'b0), .clk(Clock), .R(Clock), .Q(wr_com), .Qn(s_r_ff_2_qn), .preset(and_9_out));  // open: reset, en
  not not_8 (not_8_out, s_r_ff_2_qn);
  write_offset write_offset_1 (
    .clock(Clock), .reset(sent_done), .address(command_address), .data(command_data), .ofs_done(ofs_done),
    .ofs_ld(ofs_ld));
  and and_10 (run_prog, s_r_ff_2_qn, not_8_out);
  generator generator_1 (
    .clock(Clock), .reset(reset), .data(command_data), .address(command_address), .gen_done(gen_done),
    .gen_ld(gen_ld));

  // Other names for the same wires on the sheet: RAM_data[7:0] = card_value; gen_address[7:0] = command_address;
  //   IO_address[7:0] = command_address; ofs_address[7:0] = command_address; sent_address[7:0] = command_address;
  //   gen_data[7:0] = command_data; IO_data[7:0] = command_data; ofs_data[7:0] = command_data;
  //   sent_data[7:0] = command_data

  // Notes on the sheet:
  //   Value reading
  //   Card printer
  //   Updating indicators
  //   contents of rom_1 (hex, n*v repeats v):
  //   cc 10 c1 d1 a c1 d1 80 c1 d9 c5 d5 ee b d0 10 c1 d1 16 a4 c5 cd 0 d9 d2 f3 ba d0 f 42 d6 90 c3 d0 40
  //   bd 41 e0 2a 8f ee 23 c3 8b bd d2 f3 ba 4*9a d6 90 d0 f 41 89 89 e1 3f ee e 8d be 42 e1 46 ee e 76 e0
  //   4c 8f ee 40 d0 7f 8b be 42 ae 8f c5 d0 40 be 42 e0 63 be a6 d2 0 ae 8f 8d ee 56 c7 c3 d0 49 be 78 e1
  //   6f 8f 88 ee 67 d1 41 74 e0 76 ee e c7 8b d0 7f be 42 ae d0 40 8f be 42 e0 89 d2 0 ae ee 7f d3 f4 be
  //   8e ae ee e d3 80 8a 1b bf d0 80 8f be 42 e0 9e ee 97 d7 81*0 18
  //   from
  //   Start new game
  //   Run command
  //   Cancel command
  //   Current command
  //   to
  //   C - closed card
  //   0 - empty cell
  //   Data to/from RAM
  //   Addresses to RAM
  //   Card replacer
  //   RAM clock
  //   Read/print to RAM
  //   rising edge
  //   Full decks collected
  //   Score 4 to win
  //   Print cards to indicators
  //   Add sentinels and deck offsets
  //   Write command to RAM
  //   Generate colod
endmodule

module configuration (
  input  [31:0] colods,
  input  clock,
  input  enable,
  output [31:0] final_colod,
  output [3:0] card
);

  wire new_taken_prime;
  wire [2:0] adder_1_out;
  wire [3:3] adder_1_cout;
  wire [4:0] new_card;
  wire [31:0] pull_resistor_1_node, shifter_1_out;

  Random #(.width(5)) random_1 (.clk(clock), .next(enable), .out(new_card));  // open: clr
  // Probe on new_card
  Multiplexer #(.select(5), .enable("false")) multiplexer_1 (
    .in0(colods[0]), .in1(colods[1]), .in2(colods[2]), .in3(colods[3]), .in4(colods[4]), .in5(colods[5]),
    .in6(colods[6]), .in7(colods[7]), .in8(colods[8]), .in9(colods[9]), .in10(colods[10]), .in11(colods[11]),
    .in12(colods[12]), .in13(colods[13]), .in14(colods[14]), .in15(colods[15]), .in16(colods[16]),
    .in17(colods[17]), .in18(colods[18]), .in19(colods[19]), .in20(colods[20]), .in21(colods[21]),
    .in22(colods[22]), .in23(colods[23]), .in24(colods[24]), .in25(colods[25]), .in26(colods[26]),
    .in27(colods[27]), .in28(colods[28]), .in29(colods[29]), .in30(colods[30]), .in31(colods[31]),
    .out(new_taken_prime), .sel(new_card));
  Shifter #(.width(32)) shifter_1 (.in(32'h1), .\dist (new_card), .out(shifter_1_out));
  Pull_Resistor pull_resistor_1 (.node(pull_resistor_1_node));
  assign pull_resistor_1_node = enable ? shifter_1_out : 32'bz;  // Controlled_Buffer controlled_buffer_1
  assign final_colod = ~pull_resistor_1_node & colods;  // AND_Gate and_1, 32 bits wide
  Adder #(.width(3)) adder_1 (.a(new_card[2:0]), .b(3'b010), .out(adder_1_out), .cout(adder_1_cout[3]));  // open: cin
  assign card = new_taken_prime ? {adder_1_cout[3], adder_1_out} : 4'bz;  // Controlled_Buffer controlled_buffer_2
  Pull_Resistor pull_resistor_2 (.node(card));
endmodule

module generator (
  input  clock,
  input  reset,
  output [7:0] address,
  output [7:0] data,
  output gen_done,
  output gen_ld
);

  wire card_gen, comparator_1_eq, comparator_2_eq, comparator_3_eq, comparator_4_eq, comparator_5_eq,
       comparator_6_eq, comparator_7_eq, comparator_8_eq, eq_0, gen_clock, gen_done_t, gen_in_prog,
       gen_in_prog_prime, norm_gen, not_3_out, or_2_out, start;
  wire [3:0] configuration_1_card;
  wire [4:0] counter_1_q;
  wire [7:0] addr;
  wire [7:7] not_1_out;
  wire [31:0] configuration_1_final_colod, multiplexer_2_out, register_1_q;

  S_R_Flip_Flop #(.trigger("falling")) s_r_ff_1 (
    .Q(gen_in_prog), .Qn(gen_in_prog_prime), .preset(reset), .reset(gen_done_t));  // open: S, clk, R, en
  Multiplexer #(.select(5), .width(8), .disabled(0), .enable("false")) multiplexer_1 (
    .in0(8'h91), .in1(8'h92), .in2(8'h9c), .in3(8'h9d), .in4(8'h9e), .in5(8'ha8), .in6(8'ha9), .in7(8'haa),
    .in8(8'hab), .in9(8'hb5), .in10(8'hb6), .in11(8'hb7), .in12(8'hb8), .in13(8'hb9), .in14(8'hc3),
    .in15(8'hc4), .in16(8'hc5), .in17(8'hc6), .in18(8'hc7), .in19(8'hd1), .in20(8'hd2), .in21(8'hd3),
    .in22(8'hd4), .in23(8'hd5), .in24(8'hd6), .in25(8'he0), .in26(8'he1), .in27(8'he2), .in28(8'he3),
    .in29(8'he4), .in30(8'he5), .in31(8'he6), .out(addr), .sel(counter_1_q));
  and and_1 (gen_clock, clock, gen_in_prog);
  and and_2 (norm_gen, card_gen, gen_in_prog);
  or or_1 (start, clock, reset);
  Counter #(.width(5), .max('h1f)) counter_1 (
    .count(norm_gen), .Q(counter_1_q), .clk(gen_clock), .clr(reset));  // open: load, D, carry
  Comparator comparator_1 (.a(8'h92), .b(addr), .eq(comparator_1_eq));  // open: gt, lt
  Comparator comparator_2 (.a(8'h9e), .b(addr), .eq(comparator_2_eq));  // open: gt, lt
  Comparator comparator_3 (.a(8'hab), .b(addr), .eq(comparator_3_eq));  // open: gt, lt
  Comparator comparator_4 (.a(8'hb9), .b(addr), .eq(comparator_4_eq));  // open: gt, lt
  Comparator comparator_5 (.a(8'hc7), .b(addr), .eq(comparator_5_eq));  // open: gt, lt
  Comparator comparator_6 (.a(8'hd6), .b(addr), .eq(comparator_6_eq));  // open: gt, lt
  Comparator comparator_7 (.a(8'he6), .b(addr), .eq(comparator_7_eq));  // open: gt, lt
  or or_2 (or_2_out, comparator_1_eq, comparator_2_eq, comparator_3_eq, comparator_4_eq, comparator_5_eq, comparator_6_eq, comparator_7_eq);
  assign address = norm_gen ? addr : 8'bz;  // Controlled_Buffer controlled_buffer_1
  Multiplexer #(.width(32), .enable("false")) multiplexer_2 (
    .in0({32{1'b1}}), .in1(configuration_1_final_colod), .out(multiplexer_2_out), .sel(gen_in_prog));
  Register #(.width(32)) register_1 (.D(multiplexer_2_out), .Q(register_1_q), .clk(start));  // open: en, clr
  not not_1 (not_1_out[7], or_2_out);
  // Probe on configuration_1_final_colod
  assign data = norm_gen ? {not_1_out[7], 3'b100, configuration_1_card} : 8'bz;  // Controlled_Buffer controlled_buffer_2
  configuration configuration_1 (
    .clock(gen_clock), .card(configuration_1_card), .enable(gen_in_prog), .colods(register_1_q),
    .final_colod(configuration_1_final_colod));
  Hex_Digit_Display hex_digit_display_1 (.value(configuration_1_card));  // open: dp
  Comparator #(.width(4)) comparator_8 (.a(4'b0000), .b(configuration_1_card), .eq(comparator_8_eq));  // open: gt, lt
  not not_2 (card_gen, comparator_8_eq);
  Comparator #(.width(32)) comparator_9 (.a({32{1'b0}}), .b(configuration_1_final_colod), .eq(eq_0));  // open: gt, lt
  and and_3 (gen_done, gen_in_prog_prime, not_3_out);
  not not_3 (not_3_out, gen_in_prog_prime);
  assign gen_ld = norm_gen ? gen_in_prog : 1'bz;  // Controlled_Buffer controlled_buffer_3
  and and_4 (gen_done_t, eq_0, ~card_gen);  // AND_Gate

  // Notes on the sheet:
  //   1 colon
  //   2 colon
  //   3 colon
  //   4 colon
  //   5 colon
  //   6 colon
  //   7 colon
  //   opened
  //   sentinels
  //   Chooses random card from colod
endmodule

module write_sentinels (
  input  clock,
  input  reset,
  output [7:0] address,
  output [7:0] data,
  output sent_done,
  output sent_ld
);

  wire all_cols, not_1_out, sen_done, sen_in_prog, sen_in_prog_prime, write_sent;
  wire [2:0] counter_1_q;
  wire [7:0] addr;

  S_R_Flip_Flop #(.trigger("falling")) s_r_ff_1 (
    .Q(sen_in_prog), .Qn(sen_in_prog_prime), .preset(reset), .reset(sen_done));  // open: S, clk, R, en
  Multiplexer #(.select(3), .width(8), .disabled(0), .enable("false")) multiplexer_1 (
    .in0(8'h90), .in1(8'h9b), .in2(8'ha7), .in3(8'hb4), .in4(8'hc2), .in5(8'hd0), .in6(8'hdf), .out(addr),
    .sel(counter_1_q));  // open: in7
  Counter #(.width(3), .max('h7)) counter_1 (
    .count(sen_in_prog), .Q(counter_1_q), .clk(clock), .clr(reset));  // open: load, D, carry
  and and_1 (write_sent, ~clock, sen_in_prog);  // AND_Gate
  assign address = write_sent ? addr : 8'bz;  // Controlled_Buffer controlled_buffer_1
  Comparator #(.width(3), .mode("unsigned")) comparator_1 (.a(3'b111), .b(counter_1_q), .eq(all_cols));  // open: gt, lt
  assign data = write_sent ? 8'ha : 8'bz;  // Controlled_Buffer controlled_buffer_2
  and and_2 (sen_done, all_cols, ~clock);  // AND_Gate
  not not_1 (not_1_out, sen_in_prog_prime);
  assign sent_ld = sen_in_prog ? write_sent : 1'bz;  // Controlled_Buffer controlled_buffer_3
  and and_3 (sent_done, sen_in_prog_prime, not_1_out);

  // Notes on the sheet:
  //   sentinels
endmodule

module print_cards (
  input  clock,
  input  start,
  output [7:0] adr,
  output print_sel,
  output print_r,
  output print_done
);

  wire and_4_out, main_done, main_in_prog, not_1_out, or_1_out, pr_in_prog, win_in_prog;
  wire [7:0] counter_1_q;

  S_R_Flip_Flop #(.trigger("falling")) s_r_ff_1 (
    .S(1'b0), .clk(clock), .R(print_done), .Q(pr_in_prog), .preset(start));  // open: Qn, reset, en
  Counter counter_1 (.load(1'b1), .D(8'hee), .count(main_in_prog), .Q(counter_1_q), .clk(clock));  // open: carry, clr
  assign adr = win_in_prog ? 8'hf4 : 8'bz;  // Controlled_Buffer controlled_buffer_1
  assign adr = main_in_prog ? counter_1_q : 8'bz;  // Controlled_Buffer controlled_buffer_2
  and and_1 (main_done, ~counter_1_q[0], ~counter_1_q[1], ~counter_1_q[2], ~counter_1_q[3], counter_1_q[4], ~counter_1_q[5], ~counter_1_q[6], counter_1_q[7]);  // AND_Gate
  and and_2 (main_in_prog, pr_in_prog, ~main_done);  // AND_Gate
  and and_3 (win_in_prog, pr_in_prog, main_done);
  S_R_Flip_Flop s_r_ff_2 (
    .S(win_in_prog), .clk(clock), .R(1'b0), .Q(print_done), .reset(or_1_out));  // open: Qn, preset, en
  or or_1 (or_1_out, start, and_4_out);
  not not_1 (not_1_out, pr_in_prog);
  assign print_sel = pr_in_prog ? pr_in_prog : 1'bz;  // Controlled_Buffer controlled_buffer_3
  assign print_r = pr_in_prog ? ~pr_in_prog : 1'bz;  // Controlled_Inverter controlled_inverter_1
  and and_4 (and_4_out, pr_in_prog, not_1_out);

  // Other names for the same wires on the sheet: pr_done = print_done

  // Notes on the sheet:
  //   sentinels
  //   cards
  //   if = 0x90
endmodule

module card_replace (
  input  [2:0] colod_number,
  input  [7:0] cur_command,
  output [7:0] updated_program,
  output move_done_updated
);

  wire _1st_done, _2st_done, and_1_out, and_2_out, and_3_out, and_4_out, and_5_out, and_6_out, and_7_out,
       and_8_out, colod_isnt_0, comparator_1_eq, not_equal, or_3_out, or_4_out;

  Comparator #(.width(3), .mode("unsigned")) comparator_1 (
    .a(colod_number), .b(3'b000), .eq(comparator_1_eq));  // open: gt, lt
  not not_1 (colod_isnt_0, comparator_1_eq);
  Comparator #(.width(3), .mode("unsigned")) comparator_2 (
    .a(colod_number), .b(cur_command[2:0]), .eq(not_equal));  // open: gt, lt
  or or_1 (_1st_done, cur_command[0], cur_command[1], cur_command[2], cur_command[3]);
  or or_2 (_2st_done, cur_command[4], cur_command[5], cur_command[6], cur_command[7]);
  and and_1 (and_1_out, _1st_done, _2st_done);
  or or_3 (or_3_out, updated_program[0], updated_program[1], updated_program[2], updated_program[3]);
  and and_2 (and_2_out, or_3_out, or_4_out);
  or or_4 (or_4_out, updated_program[4], updated_program[5], updated_program[6], updated_program[7]);
  or or_5 (move_done_updated, and_1_out, and_2_out);
  and and_3 (and_3_out, _1st_done, colod_isnt_0, _2st_done, ~not_equal);  // AND_Gate
  and and_4 (and_4_out, _1st_done, ~colod_isnt_0, _2st_done, ~not_equal);  // AND_Gate
  and and_5 (and_5_out, _1st_done, colod_isnt_0, ~_2st_done, ~not_equal);  // AND_Gate
  and and_6 (and_6_out, ~_1st_done, colod_isnt_0, ~_2st_done, ~not_equal);  // AND_Gate
  and and_7 (and_7_out, _1st_done, ~colod_isnt_0, ~_2st_done, ~not_equal);  // AND_Gate
  and and_8 (and_8_out, ~_1st_done, ~colod_isnt_0, ~_2st_done, ~not_equal);  // AND_Gate
  assign updated_program = and_3_out ? cur_command : 8'bz;  // Controlled_Buffer controlled_buffer_1
  assign updated_program = and_4_out ? cur_command : 8'bz;  // Controlled_Buffer controlled_buffer_2
  assign updated_program = and_5_out ? {1'b0, colod_number, cur_command[3:0]} : 8'bz;  // Controlled_Buffer controlled_buffer_3
  assign updated_program = and_6_out ? {cur_command[7:4], 1'b0, colod_number} : 8'bz;  // Controlled_Buffer controlled_buffer_4
  assign updated_program = and_7_out ? cur_command : 8'bz;  // Controlled_Buffer controlled_buffer_5
  assign updated_program = and_8_out ? cur_command : 8'bz;  // Controlled_Buffer controlled_buffer_6
  assign updated_program = not_equal ? cur_command : 8'bz;  // Controlled_Buffer controlled_buffer_7

  // Other names for the same wires on the sheet: c[2:0] = colod_number;
  //   case1 (some bits) = {cur_command[7:4], colod_number}; case2[6:0] = {colod_number, cur_command[3:0]};
  //   case3[7:0] = cur_command; command[7:0] = cur_command; res[7:0] = updated_program
endmodule

module my_replace (
  input  [3:0] colod_number,
  input  enable,
  input  clock,
  input  reset,
  output [7:0] from_to,
  output com_ready
);

  wire and_1_out, wr_done, wr_from, wr_in_prog;
  wire [3:0] demultiplexer_1_out0, demultiplexer_1_out1;

  S_R_Flip_Flop #(.trigger("falling")) s_r_ff_1 (
    .Q(wr_in_prog), .preset(and_1_out), .reset(wr_done));  // open: S, clk, R, Qn, en
  and and_1 (and_1_out, enable, ~com_ready);  // AND_Gate
  Demultiplexer #(.width(4), .tristate("true")) demultiplexer_1 (
    .out0(demultiplexer_1_out0), .out1(demultiplexer_1_out1), .in(colod_number), .sel(wr_from),
    .en(wr_in_prog));
  Register #(.width(4)) register_1 (.D(demultiplexer_1_out0), .Q(from_to[3:0]), .clk(clock), .clr(reset));  // open: en
  Register #(.width(4)) register_2 (.D(demultiplexer_1_out1), .Q(from_to[7:4]), .clk(clock), .clr(reset));  // open: en
  or or_1 (wr_from, from_to[0], from_to[1], from_to[2], from_to[3]);
  or or_2 (com_ready, from_to[4], from_to[5], from_to[6], from_to[7]);
  D_Flip_Flop d_ff_1 (.clk(clock), .D(wr_in_prog), .Q(wr_done));  // open: Qn, preset, en, reset

  // Other names for the same wires on the sheet: c[3:0] = colod_number; wr_stop = com_ready

  // Notes on the sheet:
  //   to column was written
  //   from column was written
endmodule

module write_offset (
  input  clock,
  input  reset,
  output [7:0] address,
  output [7:0] data,
  output ofs_done,
  output ofs_ld
);

  wire all_cols, not_1_out, ofs_done_t, ofs_in_prog, ofs_in_prog_prime, write_ofs;
  wire [2:0] counter_1_q;
  wire [7:0] addr, bit_extender_1_out, data_t;

  S_R_Flip_Flop #(.trigger("falling")) s_r_ff_1 (
    .Q(ofs_in_prog), .Qn(ofs_in_prog_prime), .preset(reset), .reset(ofs_done_t));  // open: S, clk, R, en
  Multiplexer #(.select(3), .width(8), .disabled(0), .enable("false")) multiplexer_1 (
    .in0(8'h90), .in1(8'h9b), .in2(8'ha7), .in3(8'hb4), .in4(8'hc2), .in5(8'hd0), .in6(8'hdf), .out(data_t),
    .sel(counter_1_q));  // open: in7
  Counter #(.width(3), .max('h7)) counter_1 (
    .count(ofs_in_prog), .Q(counter_1_q), .clk(clock), .clr(reset));  // open: load, D, carry
  and and_1 (write_ofs, ~clock, ofs_in_prog);  // AND_Gate
  assign address = write_ofs ? addr : 8'bz;  // Controlled_Buffer controlled_buffer_1
  Comparator #(.width(3), .mode("unsigned")) comparator_1 (.a(3'b111), .b(counter_1_q), .eq(all_cols));  // open: gt, lt
  assign bit_extender_1_out = {{5{1'b0}}, counter_1_q};  // Bit_Extender bit_extender_1
  assign data = write_ofs ? data_t : 8'bz;  // Controlled_Buffer controlled_buffer_2
  Adder adder_1 (.a(8'h80), .b(bit_extender_1_out), .out(addr));  // open: cin, cout
  and and_2 (ofs_done_t, all_cols, ~clock);  // AND_Gate
  not not_1 (not_1_out, ofs_in_prog_prime);
  assign ofs_ld = ofs_in_prog ? write_ofs : 1'bz;  // Controlled_Buffer controlled_buffer_3
  and and_3 (ofs_done, ofs_in_prog_prime, not_1_out);
endmodule

module _128_decoder (
  input  [6:0] select,
  output _0,
  output _64,
  output _1,
  output _65,
  output _2,
  output _66,
  output _3,
  output _67,
  output _4,
  output _68,
  output _5,
  output _69,
  output _6,
  output _70,
  output _7,
  output _71,
  output _8,
  output _72,
  output _9,
  output _73,
  output _10,
  output _74,
  output _11,
  output _75,
  output _12,
  output _76,
  output _13,
  output _77,
  output _14,
  output _78,
  output _15,
  output _79,
  output _16,
  output _80,
  output _17,
  output _81,
  output _18,
  output _82,
  output _19,
  output _83,
  output _20,
  output _84,
  output _21,
  output _85,
  output _22,
  output _86,
  output _23,
  output _87,
  output _24,
  output _88,
  output _25,
  output _89,
  output _26,
  output _90,
  output _27,
  output _91,
  output _28,
  output _92,
  output _29,
  output _93,
  output _30,
  output _94,
  output _31,
  output _95,
  output _32,
  output _96,
  output _33,
  output _97,
  output _34,
  output _98,
  output _35,
  output _99,
  output _36,
  output _100,
  output _37,
  output _101,
  output _38,
  output _102,
  output _39,
  output _103,
  output _40,
  output _104,
  output _41,
  output _105,
  output _42,
  output _106,
  output _43,
  output _107,
  output _44,
  output _108,
  output _45,
  output _109,
  output _46,
  output _110,
  output _47,
  output _111,
  output _48,
  output _112,
  output _49,
  output _113,
  output _50,
  output _114,
  output _51,
  output _115,
  output _52,
  output _116,
  output _53,
  output _117,
  output _54,
  output _118,
  output _55,
  output _119,
  output _56,
  output _120,
  output _57,
  output _121,
  output _58,
  output _122,
  output _59,
  output _123,
  output _60,
  output _124,
  output _61,
  output _125,
  output _62,
  output _126,
  output _63,
  output _127
);

  wire not_1_out;

  not not_1 (not_1_out, select[6]);
  _64_decoder u_64_decoder_1 (
    .select(select[5:0]), ._0(_0), ._32(_32), ._1(_1), ._33(_33), ._2(_2), ._34(_34), ._3(_3), ._35(_35),
    ._4(_4), ._36(_36), ._5(_5), ._37(_37), ._6(_6), ._38(_38), ._7(_7), ._39(_39), ._8(_8), ._40(_40),
    ._9(_9), ._41(_41), ._10(_10), ._42(_42), ._11(_11), ._43(_43), ._12(_12), ._44(_44), ._13(_13),
    ._45(_45), ._14(_14), ._46(_46), ._15(_15), ._47(_47), ._16(_16), ._48(_48), ._17(_17), ._49(_49),
    ._18(_18), ._50(_50), ._19(_19), ._51(_51), ._20(_20), ._52(_52), ._21(_21), ._53(_53), ._22(_22),
    ._54(_54), ._23(_23), ._55(_55), ._24(_24), ._56(_56), ._25(_25), ._57(_57), ._26(_26), ._58(_58),
    ._27(_27), ._59(_59), ._28(_28), ._60(_60), ._29(_29), ._61(_61), ._30(_30), ._62(_62), ._31(_31),
    ._63(_63), .enable(not_1_out));
  _64_decoder u_64_decoder_2 (
    .select(select[5:0]), ._0(_64), ._32(_96), ._1(_65), ._33(_97), ._2(_66), ._34(_98), ._3(_67), ._35(_99),
    ._4(_68), ._36(_100), ._5(_69), ._37(_101), ._6(_70), ._38(_102), ._7(_71), ._39(_103), ._8(_72),
    ._40(_104), ._9(_73), ._41(_105), ._10(_74), ._42(_106), ._11(_75), ._43(_107), ._12(_76), ._44(_108),
    ._13(_77), ._45(_109), ._14(_78), ._46(_110), ._15(_79), ._47(_111), ._16(_80), ._48(_112), ._17(_81),
    ._49(_113), ._18(_82), ._50(_114), ._19(_83), ._51(_115), ._20(_84), ._52(_116), ._21(_85), ._53(_117),
    ._22(_86), ._54(_118), ._23(_87), ._55(_119), ._24(_88), ._56(_120), ._25(_89), ._57(_121), ._26(_90),
    ._58(_122), ._27(_91), ._59(_123), ._28(_92), ._60(_124), ._29(_93), ._61(_125), ._30(_94), ._62(_126),
    ._31(_95), ._63(_127), .enable(select[6]));
endmodule

module _64_decoder (
  input  [5:0] select,
  input  enable,
  output _0,
  output _32,
  output _1,
  output _33,
  output _2,
  output _34,
  output _3,
  output _35,
  output _4,
  output _36,
  output _5,
  output _37,
  output _6,
  output _38,
  output _7,
  output _39,
  output _8,
  output _40,
  output _9,
  output _41,
  output _10,
  output _42,
  output _11,
  output _43,
  output _12,
  output _44,
  output _13,
  output _45,
  output _14,
  output _46,
  output _15,
  output _47,
  output _16,
  output _48,
  output _17,
  output _49,
  output _18,
  output _50,
  output _19,
  output _51,
  output _20,
  output _52,
  output _21,
  output _53,
  output _22,
  output _54,
  output _23,
  output _55,
  output _24,
  output _56,
  output _25,
  output _57,
  output _26,
  output _58,
  output _27,
  output _59,
  output _28,
  output _60,
  output _29,
  output _61,
  output _30,
  output _62,
  output _31,
  output _63
);

  wire and_1_out, and_2_out;

  Decoder #(.select(5), .disabled(0)) decoder_1 (
    .out0(_0), .out1(_1), .out2(_2), .out3(_3), .out4(_4), .out5(_5), .out6(_6), .out7(_7), .out8(_8),
    .out9(_9), .out10(_10), .out11(_11), .out12(_12), .out13(_13), .out14(_14), .out15(_15), .out16(_16),
    .out17(_17), .out18(_18), .out19(_19), .out20(_20), .out21(_21), .out22(_22), .out23(_23), .out24(_24),
    .out25(_25), .out26(_26), .out27(_27), .out28(_28), .out29(_29), .out30(_30), .out31(_31),
    .sel(select[4:0]), .en(and_1_out));
  and and_1 (and_1_out, ~select[5], enable);  // AND_Gate
  and and_2 (and_2_out, select[5], enable);
  Decoder #(.select(5), .disabled(0)) decoder_2 (
    .out0(_32), .out1(_33), .out2(_34), .out3(_35), .out4(_36), .out5(_37), .out6(_38), .out7(_39),
    .out8(_40), .out9(_41), .out10(_42), .out11(_43), .out12(_44), .out13(_45), .out14(_46), .out15(_47),
    .out16(_48), .out17(_49), .out18(_50), .out19(_51), .out20(_52), .out21(_53), .out22(_54), .out23(_55),
    .out24(_56), .out25(_57), .out26(_58), .out27(_59), .out28(_60), .out29(_61), .out30(_62), .out31(_63),
    .sel(select[4:0]), .en(and_2_out));
endmodule
