// Logisim project myirq_done.circ as structural Verilog: 1 circuit, main circuit main
module main (
);

  wire and_1_out, button_1_out, cdm_8_mark5_1_p3, cdm_8_mark5_1_p5, cdm_8_mark5_1_p7, cdm_8_mark5_1_p8, Cl,
       code, d_ff_1_q, data, mem, not_1_out, not_2_out, not_3_out, rd_wr_prime;
  wire [7:0] cdm_8_mark5_1_p11, cdm_8_mark5_1_p12, cdm_8_mark5_1_p13, controlled_buffer_2_out;

  D_Flip_Flop d_ff_1 (.Q(d_ff_1_q), .preset(button_1_out), .reset(and_1_out));  // open: clk, D, Qn, en
  Button button_1 (.out(button_1_out));
  // NOT_Gate not_1 has open pins: in=open, out=not_1_out
  and and_1 (and_1_out, not_1_out, not_2_out);
  not not_2 (not_2_out, not_1_out);
  // Probe on cdm_8_mark5_1_p3
  Clock clock_1 (.out(Cl));
  // Probe on cdm_8_mark5_1_p7
  // CdM_8_mark5 cdm_8_mark5_1: pin names not known; wires that end beside it: d_ff_1_q, 3'b000, cdm_8_mark5_1_p3, Cl, cdm_8_mark5_1_p5, cdm_8_mark5_1_p5, cdm_8_mark5_1_p7, cdm_8_mark5_1_p8, mem, rd_wr_prime, cdm_8_mark5_1_p11, cdm_8_mark5_1_p12, cdm_8_mark5_1_p13
  Decoder #(.disabled(0)) decoder_1 (.out0(code), .out1(data), .sel(cdm_8_mark5_1_p8), .en(mem));
  not not_3 (not_3_out, rd_wr_prime);
  assign cdm_8_mark5_1_p13 = rd_wr_prime ? controlled_buffer_2_out : 8'bz;  // Controlled_Buffer controlled_buffer_1
  assign controlled_buffer_2_out = not_3_out ? cdm_8_mark5_1_p12 : 8'bz;  // Controlled_Buffer controlled_buffer_2
  // Probe on cdm_8_mark5_1_p11
  ROM rom_1 (.addr(cdm_8_mark5_1_p11), .data(controlled_buffer_2_out), .sel(code));
  RAM ram_1 (
    .addr(cdm_8_mark5_1_p11), .data(controlled_buffer_2_out), .sel(data), .clk(Cl), .ld(rd_wr_prime));  // open: clr
  // Probe on controlled_buffer_2_out

  // Notes on the sheet:
  //   contents of rom_1 (hex, n*v repeats v):
  //   cc 10 c1 d1 a c1 d1 80 c1 d9 c5
endmodule
