// Logisim project solitaire.circ as structural Verilog: 8 circuits, main circuit main
module main (
);

  wire _1colod, _2colod, _3colod, _4colod, _5colod, _6colod, _7colod, _9a_e, _9b_e, _9c_e, _9d_e, _9e_e,
       _9f_e, _91_e, _92_e, _93_e, _94_e, _95_e, _96_e, _97_e, _98_e, a0_e, a1_e, a2_e, a4_e, a5_e, a6_e,
       a7_e, a8_e, a9_e, aa_e, ab_e, ac_e, ad_e, af_e, and_1_out, and_3_out, and_4_out, and_7_out, and_9_out,
       b0_e, b1_e, b2_e, b3_e, b4_e, b5_e, b6_e, b7_e, b8_e, b9_e, bb_e, bc_e, bd_e, be_e, bf_e, c0_e, c1_e,
       c2_e, c3_e, c4_e, c5_e, c6_e, c8_e, c9_e, ca_e, cancel_com, cb_e, cc_e, cd_e, cdm_8_mark5_1_p3,
       cdm_8_mark5_1_p4, cdm_8_mark5_1_p6, cdm_8_mark5_1_p7, cdm_8_mark5_1_p9, cdm_8_mark5_1_p10, ce_e, cf_e,
       Clock, clr_com, code, com_enable, command_ld, comparator_2_gt, d0_e, d1_e, d2_e, d3_e, d4_e, d6_e,
       d7_e, d8_e, d9_e, d_ff_1_q, da_e, data, db_e, dc_e, dd_e, de_e, df_e, disp_ready, drag_in_pr, e0_e,
       e1_e, e2_e, e3_e, gen_done, gen_ld, IO_out_in_prime, IO_sel, memory, new_turn, not_1_out, not_2_out,
       not_3_out, not_4_out, not_5_out, not_6_out, not_8_out, not_9_out, ofs_done, ofs_ld, or_4_out, print_r,
       print_sel, pull_resistor_2_node, RAM_r_wr_prime, RAM_sel, read_write, reset, run_com, run_command,
       run_prog, s_r_ff_2_qn, sent_done, sent_ld, start_game, wr_com, wr_enable, wr_enable_prime;
  wire [3:0] _9a, _9b, _9c, _9d, _9e, _9f, _91, _92, _93, _94, _95, _96, _97, _98, a0, a1, a2, a4, a5, a6,
       a7, a8, a9, aa, ab, ac, ad, af, b0, b1, b2, b3, b4, b5, b6, b7, b8, b9, bb, bc, bd, be, bf, c0, c1,
       c2, c3, c4, c5, c6, c8, c9, ca, cb, cc, cd, ce, cf, com_value, d0, d1, d2, d3, d4, d6, d7, d8, d9, da,
       db, dc, dd, de, df, e0, e1, e2, e3, value;
  wire [4:0] bit_extender_1_out, bit_extender_2_out, bit_extender_3_out;
  wire [7:0] addr, card_value, cdm_8_mark5_1_p14, cdm_8_mark5_1_p15, command_address, command_data,
       current_command, data_base, pc, print_address, RAM_address, subtractor_1_out, subtractor_2_out,
       subtractor_3_out;

  // Probe on addr
  buf buffer_1 (IO_sel, gen_ld);
  buf buffer_2 (IO_out_in_prime, gen_ld);
  buf buffer_3 (IO_sel, sent_ld);
  buf buffer_4 (IO_out_in_prime, sent_ld);
  buf buffer_5 (IO_sel, print_sel);
  buf buffer_6 (IO_out_in_prime, print_r);
  buf buffer_7 (IO_sel, command_ld);
  buf buffer_8 (IO_out_in_prime, command_ld);
  buf buffer_9 (IO_sel, ofs_ld);
  buf buffer_10 (IO_out_in_prime, ofs_ld);
  D_Flip_Flop d_ff_1 (.Q(d_ff_1_q), .preset(run_prog), .reset(and_1_out));  // open: clk, D, Qn, en
  and and_1 (and_1_out, not_1_out, not_2_out);
  Register #(.width(4), .trigger("falling")) register_1 (.D(value), .en(_91_e), .Q(_91), .clk(Clock));  // open: clr
  Register #(.width(4), .trigger("falling")) register_2 (.D(value), .en(_92_e), .Q(_92), .clk(Clock));  // open: clr
  Register #(.width(4), .trigger("falling")) register_3 (.D(value), .en(_93_e), .Q(_93), .clk(Clock));  // open: clr
  Register #(.width(4), .trigger("falling")) register_4 (.D(value), .en(_94_e), .Q(_94), .clk(Clock));  // open: clr
  Register #(.width(4), .trigger("falling")) register_5 (.D(value), .en(_95_e), .Q(_95), .clk(Clock));  // open: clr
  Register #(.width(4), .trigger("falling")) register_6 (.D(value), .en(_96_e), .Q(_96), .clk(Clock));  // open: clr
  Register #(.width(4), .trigger("falling")) register_7 (.D(value), .en(_97_e), .Q(_97), .clk(Clock));  // open: clr
  Register #(.width(4), .trigger("falling")) register_8 (.D(value), .en(_98_e), .Q(_98), .clk(Clock));  // open: clr
  Multiplexer #(.width(4), .enable("false")) multiplexer_1 (
    .in0(card_value[3:0]), .in1(4'b1100), .out(value), .sel(card_value[7]));
  // Probe on cdm_8_mark5_1_p4
  // Probe on cdm_8_mark5_1_p3
  // NOT_Gate not_1 has open pins: in=open, out=not_1_out
  not not_2 (not_2_out, not_1_out);
  // Probe on data_base
  ROM rom_1 (.addr(addr), .data(data_base), .sel(code));
  assign command_address = print_address;  // Buffer buffer_11, 8 bits wide
  // Probe on cdm_8_mark5_1_p6
  // Probe on cdm_8_mark5_1_p7
  Clock clock_1 (.out(Clock));
  Register #(.width(4), .trigger("falling")) register_9 (.D(value), .en(_9a_e), .Q(_9a), .clk(Clock));  // open: clr
  Register #(.width(4), .trigger("falling")) register_10 (.D(value), .en(_9b_e), .Q(_9b), .clk(Clock));  // open: clr
  Register #(.width(4), .trigger("falling")) register_11 (.D(value), .en(_9c_e), .Q(_9c), .clk(Clock));  // open: clr
  Register #(.width(4), .trigger("falling")) register_12 (.D(value), .en(_9d_e), .Q(_9d), .clk(Clock));  // open: clr
  Register #(.width(4), .trigger("falling")) register_13 (.D(value), .en(_9e_e), .Q(_9e), .clk(Clock));  // open: clr
  Register #(.width(4), .trigger("falling")) register_14 (.D(value), .en(_9f_e), .Q(_9f), .clk(Clock));  // open: clr
  Register #(.width(4), .trigger("falling")) register_15 (.D(value), .en(a0_e), .Q(a0), .clk(Clock));  // open: clr
  Register #(.width(4), .trigger("falling")) register_16 (.D(value), .en(a1_e), .Q(a1), .clk(Clock));  // open: clr
  Register #(.width(4), .trigger("falling")) register_17 (.D(value), .en(a2_e), .Q(a2), .clk(Clock));  // open: clr
  // Probe on cdm_8_mark5_1_p9
  // CdM_8_mark5 cdm_8_mark5_1: pin names not known; wires that end beside it: d_ff_1_q, 3'b000, cdm_8_mark5_1_p3, cdm_8_mark5_1_p4, Clock, cdm_8_mark5_1_p6, cdm_8_mark5_1_p7, pc, cdm_8_mark5_1_p9, cdm_8_mark5_1_p10, memory, read_write, addr, cdm_8_mark5_1_p14, cdm_8_mark5_1_p15
  assign cdm_8_mark5_1_p15 = read_write ? data_base : 8'bz;  // Controlled_Buffer controlled_buffer_1
  Decoder #(.disabled(0)) decoder_1 (.out0(code), .out1(data), .sel(cdm_8_mark5_1_p10), .en(memory));
  assign data_base = not_3_out ? cdm_8_mark5_1_p14 : 8'bz;  // Controlled_Buffer controlled_buffer_2
  not not_3 (not_3_out, read_write);
  // Probe on RAM_address
  Register #(.width(4), .trigger("falling")) register_18 (.D(value), .en(a4_e), .Q(a4), .clk(Clock));  // open: clr
  Register #(.width(4), .trigger("falling")) register_19 (.D(value), .en(a5_e), .Q(a5), .clk(Clock));  // open: clr
  Register #(.width(4), .trigger("falling")) register_20 (.D(value), .en(a6_e), .Q(a6), .clk(Clock));  // open: clr
  Register #(.width(4), .trigger("falling")) register_21 (.D(value), .en(a7_e), .Q(a7), .clk(Clock));  // open: clr
  Register #(.width(4), .trigger("falling")) register_22 (.D(value), .en(a8_e), .Q(a8), .clk(Clock));  // open: clr
  Register #(.width(4), .trigger("falling")) register_23 (.D(value), .en(a9_e), .Q(a9), .clk(Clock));  // open: clr
  Register #(.width(4), .trigger("falling")) register_24 (.D(value), .en(aa_e), .Q(aa), .clk(Clock));  // open: clr
  Register #(.width(4), .trigger("falling")) register_25 (.D(value), .en(ab_e), .Q(ab), .clk(Clock));  // open: clr
  Register #(.width(4), .trigger("falling")) register_26 (.D(value), .en(ac_e), .Q(ac), .clk(Clock));  // open: clr
  Register #(.width(4), .trigger("falling")) register_27 (.D(value), .en(ad_e), .Q(ad), .clk(Clock));  // open: clr
  RAM ram_1 (.addr(RAM_address), .data(card_value), .sel(RAM_sel), .clk(Clock), .ld(RAM_r_wr_prime), .clr(reset));
  Pull_Resistor pull_resistor_1 (.node(IO_sel));
  Register #(.width(4), .trigger("falling")) register_28 (.D(value), .en(af_e), .Q(af), .clk(Clock));  // open: clr
  Register #(.width(4), .trigger("falling")) register_29 (.D(value), .en(b0_e), .Q(b0), .clk(Clock));  // open: clr
  Register #(.width(4), .trigger("falling")) register_30 (.D(value), .en(b1_e), .Q(b1), .clk(Clock));  // open: clr
  Register #(.width(4), .trigger("falling")) register_31 (.D(value), .en(b2_e), .Q(b2), .clk(Clock));  // open: clr
  Register #(.width(4), .trigger("falling")) register_32 (.D(value), .en(b3_e), .Q(b3), .clk(Clock));  // open: clr
  Register #(.width(4), .trigger("falling")) register_33 (.D(value), .en(b4_e), .Q(b4), .clk(Clock));  // open: clr
  Register #(.width(4), .trigger("falling")) register_34 (.D(value), .en(b5_e), .Q(b5), .clk(Clock));  // open: clr
  Register #(.width(4), .trigger("falling")) register_35 (.D(value), .en(b6_e), .Q(b6), .clk(Clock));  // open: clr
  Register #(.width(4), .trigger("falling")) register_36 (.D(value), .en(b7_e), .Q(b7), .clk(Clock));  // open: clr
  Register #(.width(4), .trigger("falling")) register_37 (.D(value), .en(b8_e), .Q(b8), .clk(Clock));  // open: clr
  Register #(.width(4), .trigger("falling")) register_38 (.D(value), .en(b9_e), .Q(b9), .clk(Clock));  // open: clr
  // Probe on card_value
  Register #(.width(4), .trigger("falling")) register_39 (.D(value), .en(bb_e), .Q(bb), .clk(Clock));  // open: clr
  Register #(.width(4), .trigger("falling")) register_40 (.D(value), .en(bc_e), .Q(bc), .clk(Clock));  // open: clr
  Register #(.width(4), .trigger("falling")) register_41 (.D(value), .en(bd_e), .Q(bd), .clk(Clock));  // open: clr
  Register #(.width(4), .trigger("falling")) register_42 (.D(value), .en(be_e), .Q(be), .clk(Clock));  // open: clr
  Register #(.width(4), .trigger("falling")) register_43 (.D(value), .en(bf_e), .Q(bf), .clk(Clock));  // open: clr
  Register #(.width(4), .trigger("falling")) register_44 (.D(value), .en(c0_e), .Q(c0), .clk(Clock));  // open: clr
  Register #(.width(4), .trigger("falling")) register_45 (.D(value), .en(c1_e), .Q(c1), .clk(Clock));  // open: clr
  Register #(.width(4), .trigger("falling")) register_46 (.D(value), .en(c2_e), .Q(c2), .clk(Clock));  // open: clr
  Register #(.width(4), .trigger("falling")) register_47 (.D(value), .en(c3_e), .Q(c3), .clk(Clock));  // open: clr
  Register #(.width(4), .trigger("falling")) register_48 (.D(value), .en(c4_e), .Q(c4), .clk(Clock));  // open: clr
  Register #(.width(4), .trigger("falling")) register_49 (.D(value), .en(c5_e), .Q(c5), .clk(Clock));  // open: clr
  Register #(.width(4), .trigger("falling")) register_50 (.D(value), .en(c6_e), .Q(c6), .clk(Clock));  // open: clr
  and and_2 (reset, ~drag_in_pr, disp_ready, start_game);  // AND_Gate
  S_R_Flip_Flop s_r_ff_1 (.Qn(drag_in_pr), .preset(new_turn), .reset(run_prog));  // open: S, clk, R, Q, en
  and and_3 (and_3_out, ~IO_sel, read_write);  // AND_Gate
  assign data_base = and_3_out ? card_value : 8'bz;  // Controlled_Buffer controlled_buffer_3
  assign card_value = and_4_out ? data_base : 8'bz;  // Controlled_Buffer controlled_buffer_4
  and and_4 (and_4_out, ~IO_sel, ~read_write);  // AND_Gate
  Register #(.width(4), .trigger("falling")) register_51 (.D(value), .en(c8_e), .Q(c8), .clk(Clock));  // open: clr
  Register #(.width(4), .trigger("falling")) register_52 (.D(value), .en(c9_e), .Q(c9), .clk(Clock));  // open: clr
  Register #(.width(4), .trigger("falling")) register_53 (.D(value), .en(ca_e), .Q(ca), .clk(Clock));  // open: clr
  Register #(.width(4), .trigger("falling")) register_54 (.D(value), .en(cb_e), .Q(cb), .clk(Clock));  // open: clr
  Register #(.width(4), .trigger("falling")) register_55 (.D(value), .en(cc_e), .Q(cc), .clk(Clock));  // open: clr
  Register #(.width(4), .trigger("falling")) register_56 (.D(value), .en(cd_e), .Q(cd), .clk(Clock));  // open: clr
  Register #(.width(4), .trigger("falling")) register_57 (.D(value), .en(ce_e), .Q(ce), .clk(Clock));  // open: clr
  Register #(.width(4), .trigger("falling")) register_58 (.D(value), .en(cf_e), .Q(cf), .clk(Clock));  // open: clr
  Register #(.width(4), .trigger("falling")) register_59 (.D(value), .en(d0_e), .Q(d0), .clk(Clock));  // open: clr
  Register #(.width(4), .trigger("falling")) register_60 (.D(value), .en(d1_e), .Q(d1), .clk(Clock));  // open: clr
  Register #(.width(4), .trigger("falling")) register_61 (.D(value), .en(d2_e), .Q(d2), .clk(Clock));  // open: clr
  Register #(.width(4), .trigger("falling")) register_62 (.D(value), .en(d3_e), .Q(d3), .clk(Clock));  // open: clr
  Register #(.width(4), .trigger("falling")) register_63 (.D(value), .en(d4_e), .Q(d4), .clk(Clock));  // open: clr
  and and_5 (new_turn, pc[0], pc[1], ~pc[2], pc[3], ~pc[4], ~pc[5], ~pc[6], ~pc[7]);  // AND_Gate
  or or_1 (RAM_sel, IO_sel, data);
  Multiplexer #(.enable("false")) multiplexer_2 (.in0(read_write), .in1(not_4_out), .out(RAM_r_wr_prime), .sel(IO_sel));
  not not_4 (not_4_out, IO_out_in_prime);
  Multiplexer #(.width(8), .enable("false")) multiplexer_3 (
    .in0(addr), .in1(command_address), .out(RAM_address), .sel(IO_sel));
  assign card_value = IO_sel ? command_data : 8'bz;  // Controlled_Buffer controlled_buffer_5
  Register #(.width(4), .trigger("falling")) register_64 (.D(value), .en(d6_e), .Q(d6), .clk(Clock));  // open: clr
  Register #(.width(4), .trigger("falling")) register_65 (.D(value), .en(d7_e), .Q(d7), .clk(Clock));  // open: clr
  Register #(.width(4), .trigger("falling")) register_66 (.D(value), .en(d8_e), .Q(d8), .clk(Clock));  // open: clr
  Register #(.width(4), .trigger("falling")) register_67 (.D(value), .en(d9_e), .Q(d9), .clk(Clock));  // open: clr
  Register #(.width(4), .trigger("falling")) register_68 (.D(value), .en(da_e), .Q(da), .clk(Clock));  // open: clr
  Register #(.width(4), .trigger("falling")) register_69 (.D(value), .en(db_e), .Q(db), .clk(Clock));  // open: clr
  Register #(.width(4), .trigger("falling")) register_70 (.D(value), .en(dc_e), .Q(dc), .clk(Clock));  // open: clr
  Register #(.width(4), .trigger("falling")) register_71 (.D(value), .en(dd_e), .Q(dd), .clk(Clock));  // open: clr
  Register #(.width(4), .trigger("falling")) register_72 (.D(value), .en(de_e), .Q(de), .clk(Clock));  // open: clr
  Register #(.width(4), .trigger("falling")) register_73 (.D(value), .en(df_e), .Q(df), .clk(Clock));  // open: clr
  Register #(.width(4), .trigger("falling")) register_74 (.D(value), .en(e0_e), .Q(e0), .clk(Clock));  // open: clr
  Register #(.width(4), .trigger("falling")) register_75 (.D(value), .en(e1_e), .Q(e1), .clk(Clock));  // open: clr
  Register #(.width(4), .trigger("falling")) register_76 (.D(value), .en(e2_e), .Q(e2), .clk(Clock));  // open: clr
  Register #(.width(4), .trigger("falling")) register_77 (.D(value), .en(e3_e), .Q(e3), .clk(Clock));  // open: clr
  and and_6 (run_com, ~drag_in_pr, disp_ready, run_command);  // AND_Gate
  not not_5 (not_5_out, not_5_out);
  Pull_Resistor pull_resistor_2 (.node(pull_resistor_2_node));
  Decoder #(.select(5), .disabled(0)) decoder_2 (
    .out1(_91_e), .out2(_92_e), .out3(_93_e), .out4(_94_e), .out5(_95_e), .out6(_96_e), .out7(_97_e),
    .out8(_98_e), .out10(_9a_e), .out11(_9b_e), .out12(_9c_e), .out13(_9d_e), .out14(_9e_e), .out15(_9f_e),
    .out16(a0_e), .out17(a1_e), .out18(a2_e), .out20(a4_e), .out21(a5_e), .out22(a6_e), .out23(a7_e),
    .out24(a8_e), .out25(a9_e), .out26(aa_e), .out27(ab_e), .out28(ac_e), .out29(ad_e), .out31(af_e),
    .sel(bit_extender_1_out), .en(not_6_out));  // open: out0, out9, out19, out30
  not not_6 (not_6_out, pull_resistor_2_node);
  Comparator comparator_1 (.a(print_address), .b(8'haf), .gt(pull_resistor_2_node));  // open: eq, lt
  Subtractor subtractor_1 (.a(print_address), .b(8'h90), .out(subtractor_1_out));  // open: bin, bout
  Bit_Extender #(.out_width(5)) bit_extender_1 (.in(subtractor_1_out), .out(bit_extender_1_out));
  Pull_Resistor pull_resistor_3 (.node(bit_extender_1_out));
  assign com_value = _1colod ? 4'b0001 : 4'bz;  // Controlled_Buffer controlled_buffer_6
  assign com_value = _2colod ? 4'b0010 : 4'bz;  // Controlled_Buffer controlled_buffer_7
  assign com_value = _3colod ? 4'b0011 : 4'bz;  // Controlled_Buffer controlled_buffer_8
  assign com_value = _4colod ? 4'b0100 : 4'bz;  // Controlled_Buffer controlled_buffer_9
  assign com_value = _5colod ? 4'b0101 : 4'bz;  // Controlled_Buffer controlled_buffer_10
  assign com_value = _6colod ? 4'b0110 : 4'bz;  // Controlled_Buffer controlled_buffer_11
  assign com_value = _7colod ? 4'b0111 : 4'bz;  // Controlled_Buffer controlled_buffer_12
  Comparator comparator_2 (.a(print_address), .b(8'hce), .gt(comparator_2_gt));  // open: eq, lt
  Pull_Resistor pull_resistor_4 (.node(comparator_2_gt));
  and and_7 (and_7_out, ~comparator_2_gt, pull_resistor_2_node);  // AND_Gate
  Subtractor subtractor_2 (.a(print_address), .b(8'haf), .out(subtractor_2_out));  // open: bin, bout
  Bit_Extender #(.out_width(5)) bit_extender_2 (.in(subtractor_2_out), .out(bit_extender_2_out));
  or or_2 (clr_com, reset, cancel_com, run_prog);
  or or_3 (wr_enable_prime, _1colod, _2colod, _3colod, _4colod, _5colod, _6colod, _7colod);
  Hex_Digit_Display hex_digit_display_1 (.value(current_command[7:4]));  // open: dp
  Decoder #(.select(5), .disabled(0)) decoder_3 (
    .out1(b0_e), .out2(b1_e), .out3(b2_e), .out4(b3_e), .out5(b4_e), .out6(b5_e), .out7(b6_e), .out8(b7_e),
    .out9(b8_e), .out10(b9_e), .out12(bb_e), .out13(bc_e), .out14(bd_e), .out15(be_e), .out16(bf_e),
    .out17(c0_e), .out18(c1_e), .out19(c2_e), .out20(c3_e), .out21(c4_e), .out22(c5_e), .out23(c6_e),
    .out25(c8_e), .out26(c9_e), .out27(ca_e), .out28(cb_e), .out29(cc_e), .out30(cd_e), .out31(ce_e),
    .sel(bit_extender_2_out), .en(and_7_out));  // open: out0, out11, out24
  Pull_Resistor pull_resistor_5 (.node(bit_extender_2_out));
  Button button_1 (.out(start_game));
  Button button_2 (.out(run_command));
  Button button_3 (.out(cancel_com));
  Hex_Digit_Display hex_digit_display_2 (.value(current_command[3:0]));  // open: dp
  Subtractor subtractor_3 (.a(print_address), .b(8'hce), .out(subtractor_3_out));  // open: bin, bout
  not not_7 (not_5_out, not_5_out);
  Decoder #(.select(5), .disabled(0)) decoder_4 (
    .out1(cf_e), .out2(d0_e), .out3(d1_e), .out4(d2_e), .out5(d3_e), .out6(d4_e), .out8(d6_e), .out9(d7_e),
    .out10(d8_e), .out11(d9_e), .out12(da_e), .out13(db_e), .out14(dc_e), .out15(dd_e), .out16(de_e),
    .out17(df_e), .out18(e0_e), .out19(e1_e), .out20(e2_e), .out21(e3_e), .sel(bit_extender_3_out),
    .en(comparator_2_gt));  // open: out0, out7, out22, out23, out24, out25, out26, out27, out28, out29, out30, out31
  Bit_Extender #(.out_width(5)) bit_extender_3 (.in(subtractor_3_out), .out(bit_extender_3_out));
  Pull_Resistor pull_resistor_6 (.node(bit_extender_3_out));
  my_replace my_replace_1 (
    .colod_number(com_value), .enable(wr_enable), .clock(Clock), .from_to(current_command), .reset(clr_com),
    .com_ready(com_enable));
  not not_8 (not_8_out, wr_enable_prime);
  Button button_4 (.out(_1colod));
  Hex_Digit_Display hex_digit_display_3 (.value(_91));  // open: dp
  Hex_Digit_Display hex_digit_display_4 (.value(_92));  // open: dp
  Hex_Digit_Display hex_digit_display_5 (.value(_93));  // open: dp
  Hex_Digit_Display hex_digit_display_6 (.value(_94));  // open: dp
  Hex_Digit_Display hex_digit_display_7 (.value(_95));  // open: dp
  Hex_Digit_Display hex_digit_display_8 (.value(_96));  // open: dp
  Hex_Digit_Display hex_digit_display_9 (.value(_97));  // open: dp
  Hex_Digit_Display hex_digit_display_10 (.value(_98));  // open: dp
  and and_8 (wr_enable, wr_enable_prime, not_8_out);
  Button button_5 (.out(_2colod));
  Hex_Digit_Display hex_digit_display_11 (.value(_9a));  // open: dp
  Hex_Digit_Display hex_digit_display_12 (.value(_9b));  // open: dp
  Hex_Digit_Display hex_digit_display_13 (.value(_9c));  // open: dp
  Hex_Digit_Display hex_digit_display_14 (.value(_9d));  // open: dp
  Hex_Digit_Display hex_digit_display_15 (.value(_9e));  // open: dp
  Hex_Digit_Display hex_digit_display_16 (.value(_9f));  // open: dp
  Hex_Digit_Display hex_digit_display_17 (.value(a0));  // open: dp
  Hex_Digit_Display hex_digit_display_18 (.value(a1));  // open: dp
  Hex_Digit_Display hex_digit_display_19 (.value(a2));  // open: dp
  Button button_6 (.out(_3colod));
  Hex_Digit_Display hex_digit_display_20 (.value(a4));  // open: dp
  Hex_Digit_Display hex_digit_display_21 (.value(a5));  // open: dp
  Hex_Digit_Display hex_digit_display_22 (.value(a6));  // open: dp
  Hex_Digit_Display hex_digit_display_23 (.value(a7));  // open: dp
  Hex_Digit_Display hex_digit_display_24 (.value(a8));  // open: dp
  Hex_Digit_Display hex_digit_display_25 (.value(a9));  // open: dp
  Hex_Digit_Display hex_digit_display_26 (.value(aa));  // open: dp
  Hex_Digit_Display hex_digit_display_27 (.value(ab));  // open: dp
  Hex_Digit_Display hex_digit_display_28 (.value(ac));  // open: dp
  Hex_Digit_Display hex_digit_display_29 (.value(ad));  // open: dp
  write_sentinels write_sentinels_1 (
    .data(command_data), .clock(Clock), .reset(gen_done), .address(command_address), .sent_done(sent_done),
    .sent_ld(sent_ld));
  print_cards print_cards_1 (
    .clock(Clock), .adr(print_address), .print_sel(print_sel), .start(or_4_out), .print_r(print_r),
    .print_done(disp_ready), .reset(reset));
  or or_4 (or_4_out, ofs_done, new_turn);
  assign command_data = wr_com ? current_command : 8'bz;  // Controlled_Buffer controlled_buffer_13
  assign command_address = wr_com ? 8'hf3 : 8'bz;  // Controlled_Buffer controlled_buffer_14
  assign command_ld = wr_com ? 1'b1 : 1'bz;  // Controlled_Buffer controlled_buffer_15
  Button button_7 (.out(_4colod));
  Hex_Digit_Display hex_digit_display_30 (.value(af));  // open: dp
  Hex_Digit_Display hex_digit_display_31 (.value(b0));  // open: dp
  Hex_Digit_Display hex_digit_display_32 (.value(b1));  // open: dp
  Hex_Digit_Display hex_digit_display_33 (.value(b2));  // open: dp
  Hex_Digit_Display hex_digit_display_34 (.value(b3));  // open: dp
  Hex_Digit_Display hex_digit_display_35 (.value(b4));  // open: dp
  Hex_Digit_Display hex_digit_display_36 (.value(b5));  // open: dp
  Hex_Digit_Display hex_digit_display_37 (.value(b6));  // open: dp
  Hex_Digit_Display hex_digit_display_38 (.value(b7));  // open: dp
  Hex_Digit_Display hex_digit_display_39 (.value(b8));  // open: dp
  Hex_Digit_Display hex_digit_display_40 (.value(b9));  // open: dp
  S_R_Flip_Flop s_r_ff_2 (
    .S(1'b0), .clk(Clock), .R(Clock), .Q(wr_com), .Qn(s_r_ff_2_qn), .preset(and_9_out));  // open: reset, en
  and and_9 (and_9_out, run_com, disp_ready, com_enable);
  Button button_8 (.out(_5colod));
  Hex_Digit_Display hex_digit_display_41 (.value(bb));  // open: dp
  Hex_Digit_Display hex_digit_display_42 (.value(bc));  // open: dp
  Hex_Digit_Display hex_digit_display_43 (.value(bd));  // open: dp
  Hex_Digit_Display hex_digit_display_44 (.value(be));  // open: dp
  Hex_Digit_Display hex_digit_display_45 (.value(bf));  // open: dp
  Hex_Digit_Display hex_digit_display_46 (.value(c0));  // open: dp
  Hex_Digit_Display hex_digit_display_47 (.value(c1));  // open: dp
  Hex_Digit_Display hex_digit_display_48 (.value(c2));  // open: dp
  Hex_Digit_Display hex_digit_display_49 (.value(c3));  // open: dp
  Hex_Digit_Display hex_digit_display_50 (.value(c4));  // open: dp
  Hex_Digit_Display hex_digit_display_51 (.value(c5));  // open: dp
  Hex_Digit_Display hex_digit_display_52 (.value(c6));  // open: dp
  not not_9 (not_9_out, s_r_ff_2_qn);
  Button button_9 (.out(_6colod));
  Hex_Digit_Display hex_digit_display_53 (.value(c8));  // open: dp
  Hex_Digit_Display hex_digit_display_54 (.value(c9));  // open: dp
  Hex_Digit_Display hex_digit_display_55 (.value(ca));  // open: dp
  Hex_Digit_Display hex_digit_display_56 (.value(cb));  // open: dp
  Hex_Digit_Display hex_digit_display_57 (.value(cc));  // open: dp
  Hex_Digit_Display hex_digit_display_58 (.value(cd));  // open: dp
  Hex_Digit_Display hex_digit_display_59 (.value(ce));  // open: dp
  Hex_Digit_Display hex_digit_display_60 (.value(cf));  // open: dp
  Hex_Digit_Display hex_digit_display_61 (.value(d0));  // open: dp
  Hex_Digit_Display hex_digit_display_62 (.value(d1));  // open: dp
  Hex_Digit_Display hex_digit_display_63 (.value(d2));  // open: dp
  Hex_Digit_Display hex_digit_display_64 (.value(d3));  // open: dp
  Hex_Digit_Display hex_digit_display_65 (.value(d4));  // open: dp
  and and_10 (run_prog, s_r_ff_2_qn, not_9_out);
  Button button_10 (.out(_7colod));
  Hex_Digit_Display hex_digit_display_66 (.value(d6));  // open: dp
  Hex_Digit_Display hex_digit_display_67 (.value(d7));  // open: dp
  Hex_Digit_Display hex_digit_display_68 (.value(d8));  // open: dp
  Hex_Digit_Display hex_digit_display_69 (.value(d9));  // open: dp
  Hex_Digit_Display hex_digit_display_70 (.value(da));  // open: dp
  Hex_Digit_Display hex_digit_display_71 (.value(db));  // open: dp
  Hex_Digit_Display hex_digit_display_72 (.value(dc));  // open: dp
  Hex_Digit_Display hex_digit_display_73 (.value(dd));  // open: dp
  Hex_Digit_Display hex_digit_display_74 (.value(de));  // open: dp
  Hex_Digit_Display hex_digit_display_75 (.value(df));  // open: dp
  Hex_Digit_Display hex_digit_display_76 (.value(e0));  // open: dp
  Hex_Digit_Display hex_digit_display_77 (.value(e1));  // open: dp
  Hex_Digit_Display hex_digit_display_78 (.value(e2));  // open: dp
  Hex_Digit_Display hex_digit_display_79 (.value(e3));  // open: dp
  write_offset write_offset_1 (
    .clock(Clock), .reset(sent_done), .address(command_address), .data(command_data), .ofs_done(ofs_done),
    .ofs_ld(ofs_ld));
  generator generator_1 (
    .clock(Clock), .reset(reset), .data(command_data), .address(command_address), .gen_done(gen_done),
    .gen_ld(gen_ld));

  // Other names for the same wires on the sheet: RAM_data[7:0] = card_value; gen_address[7:0] = command_address;
  //   IO_address[7:0] = command_address; ofs_address[7:0] = command_address; sent_address[7:0] = command_address;
  //   gen_data[7:0] = command_data; IO_data[7:0] = command_data; ofs_data[7:0] = command_data;
  //   sent_data[7:0] = command_data

  // Notes on the sheet:
  //   Value reading
  //   ROM
  //   contents of rom_1 (hex, n*v repeats v):
  //   cc 10 c1 d1 a c1 d1 80 c1 d9 c5 d5 ee b d0 10 c1 d1 16 a4 c5 cd 0 d9 d2 f3 ba d0 f 42 d6 64 d0 40 bd
  //   41 e0 29 8f ee 22 c3 8b bd d2 f3 ba 4*9a d6 64 d0 f 41 89 89 e1 3e ee e 8d be 42 e1 45 ee e 76 e0 4b
  //   8f ee 3f d0 7f 8b be 42 ae 8f c5 d0 40 be 42 e0 62 be a6 d2 0 ae 8f 8d ee 55 ee e d3 80 8a 1b bf d0
  //   80 8f be 42 e0 72 ee 6b d7 125*0 18
  //   RAM
  //   Card printer
  //   Updating indicators
  //   Data bus
  //   Address bus 
  //   Reset
  //   Run cdm8 program
  //   Connection to RAM
  //   Run command
  //   Check new turn
  //   with a deck of 28 cards.
  //   ascending order into 4 cells
  //   move card or cards
  //   Fetch column number
  //   Klondike Solitaire is a card game
  //   To move cards, push button where you want to
  //   then push button where is card now
  //   If the player can no longer make any
  //   meaningful moves, the game is considered lost
  //   The goal of the game is to arrange all the cards in
  //   Choose card address
  //   Clear command register
  //   Card replacer
  //   Enable writting in command register
  //   from
  //   Solitaire
  //   Start new game
  //   Run command
  //   Cancel command
  //   Current command
  //   to
  //   C - closed card
  //   0 - empty cell
  //   Enable it asynchronously, on rising edge
  //   Print cards to indicators
  //   Add sentinels and deck offsets
  //   Write command to RAM
  //   Generate colod
endmodule

module configuration (
  input  [31:0] colods,
  input  clock,
  input  enable,
  output [31:0] final_colod,
  output [3:0] card
);

  wire new_taken_prime;
  wire [2:0] adder_1_out;
  wire [3:3] adder_1_cout;
  wire [4:0] new_card;
  wire [31:0] pull_resistor_1_node, shifter_1_out;

  // Probe on new_card
  Random #(.width(5)) random_1 (.clk(clock), .next(enable), .out(new_card));  // open: clr
  Multiplexer #(.select(5), .enable("false")) multiplexer_1 (
    .in0(colods[0]), .in1(colods[1]), .in2(colods[2]), .in3(colods[3]), .in4(colods[4]), .in5(colods[5]),
    .in6(colods[6]), .in7(colods[7]), .in8(colods[8]), .in9(colods[9]), .in10(colods[10]), .in11(colods[11]),
    .in12(colods[12]), .in13(colods[13]), .in14(colods[14]), .in15(colods[15]), .in16(colods[16]),
    .in17(colods[17]), .in18(colods[18]), .in19(colods[19]), .in20(colods[20]), .in21(colods[21]),
    .in22(colods[22]), .in23(colods[23]), .in24(colods[24]), .in25(colods[25]), .in26(colods[26]),
    .in27(colods[27]), .in28(colods[28]), .in29(colods[29]), .in30(colods[30]), .in31(colods[31]),
    .out(new_taken_prime), .sel(new_card));
  Shifter #(.width(32)) shifter_1 (.in(32'h1), .\dist (new_card), .out(shifter_1_out));
  Pull_Resistor pull_resistor_1 (.node(pull_resistor_1_node));
  assign pull_resistor_1_node = enable ? shifter_1_out : 32'bz;  // Controlled_Buffer controlled_buffer_1
  assign final_colod = ~pull_resistor_1_node & colods;  // AND_Gate and_1, 32 bits wide
  Adder #(.width(3)) adder_1 (.a(new_card[2:0]), .b(3'b010), .out(adder_1_out), .cout(adder_1_cout[3]));  // open: cin
  Pull_Resistor pull_resistor_2 (.node(card));
  assign card = new_taken_prime ? {adder_1_cout[3], adder_1_out} : 4'bz;  // Controlled_Buffer controlled_buffer_2
endmodule

module generator (
  input  clock,
  input  reset,
  output [7:0] address,
  output [7:0] data,
  output gen_done,
  output gen_ld
);

  wire card_gen, comparator_1_eq, comparator_2_eq, comparator_3_eq, comparator_4_eq, comparator_5_eq,
       comparator_6_eq, comparator_7_eq, comparator_8_eq, eq_0, gen_clock, gen_done_t, gen_in_prog,
       gen_in_prog_prime, norm_gen, not_3_out, or_2_out, start;
  wire [3:0] configuration_1_card;
  wire [4:0] counter_1_q;
  wire [7:0] addr;
  wire [7:7] not_1_out;
  wire [31:0] configuration_1_final_colod, multiplexer_2_out, register_1_q;

  S_R_Flip_Flop #(.trigger("falling")) s_r_ff_1 (
    .Q(gen_in_prog), .Qn(gen_in_prog_prime), .preset(reset), .reset(gen_done_t));  // open: S, clk, R, en
  Multiplexer #(.select(5), .width(8), .disabled(0), .enable("false")) multiplexer_1 (
    .in0(8'h91), .in1(8'h92), .in2(8'h9a), .in3(8'h9b), .in4(8'h9c), .in5(8'ha4), .in6(8'ha5), .in7(8'ha6),
    .in8(8'ha7), .in9(8'haf), .in10(8'hb0), .in11(8'hb1), .in12(8'hb2), .in13(8'hb3), .in14(8'hbb),
    .in15(8'hbc), .in16(8'hbd), .in17(8'hbe), .in18(8'hbf), .in19(8'hc8), .in20(8'hc9), .in21(8'hca),
    .in22(8'hcb), .in23(8'hcc), .in24(8'hcd), .in25(8'hd6), .in26(8'hd7), .in27(8'hd8), .in28(8'hd9),
    .in29(8'hda), .in30(8'hdb), .in31(8'hdc), .out(addr), .sel(counter_1_q));
  and and_1 (gen_clock, clock, gen_in_prog);
  and and_2 (norm_gen, card_gen, gen_in_prog);
  or or_1 (start, clock, reset);
  Counter #(.width(5), .max('h1f)) counter_1 (
    .count(norm_gen), .Q(counter_1_q), .clk(gen_clock), .clr(reset));  // open: load, D, carry
  Comparator comparator_1 (.a(8'h92), .b(addr), .eq(comparator_1_eq));  // open: gt, lt
  Comparator comparator_2 (.a(8'h9c), .b(addr), .eq(comparator_2_eq));  // open: gt, lt
  Comparator comparator_3 (.a(8'ha7), .b(addr), .eq(comparator_3_eq));  // open: gt, lt
  Comparator comparator_4 (.a(8'hb3), .b(addr), .eq(comparator_4_eq));  // open: gt, lt
  Comparator comparator_5 (.a(8'hbf), .b(addr), .eq(comparator_5_eq));  // open: gt, lt
  Comparator comparator_6 (.a(8'hcd), .b(addr), .eq(comparator_6_eq));  // open: gt, lt
  Comparator comparator_7 (.a(8'hdc), .b(addr), .eq(comparator_7_eq));  // open: gt, lt
  or or_2 (or_2_out, comparator_1_eq, comparator_2_eq, comparator_3_eq, comparator_4_eq, comparator_5_eq, comparator_6_eq, comparator_7_eq);
  assign address = norm_gen ? addr : 8'bz;  // Controlled_Buffer controlled_buffer_1
  Multiplexer #(.width(32), .enable("false")) multiplexer_2 (
    .in0({32{1'b1}}), .in1(configuration_1_final_colod), .out(multiplexer_2_out), .sel(gen_in_prog));
  Register #(.width(32)) register_1 (.D(multiplexer_2_out), .Q(register_1_q), .clk(start));  // open: en, clr
  not not_1 (not_1_out[7], or_2_out);
  // Probe on configuration_1_final_colod
  assign data = norm_gen ? {not_1_out[7], 3'b100, configuration_1_card} : 8'bz;  // Controlled_Buffer controlled_buffer_2
  configuration configuration_1 (
    .clock(gen_clock), .card(configuration_1_card), .enable(gen_in_prog), .colods(register_1_q),
    .final_colod(configuration_1_final_colod));
  Hex_Digit_Display hex_digit_display_1 (.value(configuration_1_card));  // open: dp
  Comparator #(.width(4)) comparator_8 (.a(4'b0000), .b(configuration_1_card), .eq(comparator_8_eq));  // open: gt, lt
  not not_2 (card_gen, comparator_8_eq);
  Comparator #(.width(32)) comparator_9 (.a({32{1'b0}}), .b(configuration_1_final_colod), .eq(eq_0));  // open: gt, lt
  and and_3 (gen_done, gen_in_prog_prime, not_3_out);
  not not_3 (not_3_out, gen_in_prog_prime);
  assign gen_ld = norm_gen ? gen_in_prog : 1'bz;  // Controlled_Buffer controlled_buffer_3
  and and_4 (gen_done_t, eq_0, ~card_gen);  // AND_Gate

  // Notes on the sheet:
  //   1 colon
  //   2 colon
  //   3 colon
  //   4 colon
  //   5 colon
  //   6 colon
  //   7 colon
  //   opened
  //   sentinels
  //   Chooses random card from colod
endmodule

module write_sentinels (
  input  clock,
  input  reset,
  output [7:0] address,
  output [7:0] data,
  output sent_done,
  output sent_ld
);

  wire all_cols, not_1_out, sen_done, sen_in_prog, sen_in_prog_prime, write_sent;
  wire [2:0] counter_1_q;
  wire [7:0] addr;

  S_R_Flip_Flop #(.trigger("falling")) s_r_ff_1 (
    .Q(sen_in_prog), .Qn(sen_in_prog_prime), .preset(reset), .reset(sen_done));  // open: S, clk, R, en
  Multiplexer #(.select(3), .width(8), .disabled(0), .enable("false")) multiplexer_1 (
    .in0(8'h90), .in1(8'h99), .in2(8'ha3), .in3(8'hae), .in4(8'hba), .in5(8'hc7), .in6(8'hd5), .out(addr),
    .sel(counter_1_q));  // open: in7
  Counter #(.width(3), .max('h7)) counter_1 (
    .count(sen_in_prog), .Q(counter_1_q), .clk(clock), .clr(reset));  // open: load, D, carry
  and and_1 (write_sent, ~clock, sen_in_prog);  // AND_Gate
  assign address = write_sent ? addr : 8'bz;  // Controlled_Buffer controlled_buffer_1
  Comparator #(.width(3), .mode("unsigned")) comparator_1 (.a(3'b111), .b(counter_1_q), .eq(all_cols));  // open: gt, lt
  assign data = write_sent ? 8'ha : 8'bz;  // Controlled_Buffer controlled_buffer_2
  and and_2 (sen_done, all_cols, ~clock);  // AND_Gate
  not not_1 (not_1_out, sen_in_prog_prime);
  assign sent_ld = sen_in_prog ? write_sent : 1'bz;  // Controlled_Buffer controlled_buffer_3
  and and_3 (sent_done, sen_in_prog_prime, not_1_out);

  // Notes on the sheet:
  //   opened
  //   sentinels
endmodule

module print_cards (
  input  clock,
  input  start,
  input  reset,
  output [7:0] adr,
  output print_sel,
  output print_r,
  output print_done
);

  wire or_1_out, pr_done, pr_in_prog;
  wire [7:0] counter_1_q;

  S_R_Flip_Flop #(.trigger("falling")) s_r_ff_1 (
    .Q(pr_in_prog), .preset(start), .reset(pr_done));  // open: S, clk, R, Qn, en
  Counter counter_1 (.load(1'b1), .D(8'he3), .count(pr_in_prog), .Q(counter_1_q), .clk(clock));  // open: carry, clr
  assign adr = pr_in_prog ? counter_1_q : 8'bz;  // Controlled_Buffer controlled_buffer_1
  and and_1 (pr_done, ~counter_1_q[0], ~counter_1_q[1], ~counter_1_q[2], ~counter_1_q[3], counter_1_q[4], ~counter_1_q[5], ~counter_1_q[6], counter_1_q[7]);  // AND_Gate
  assign print_sel = pr_in_prog ? pr_in_prog : 1'bz;  // Controlled_Buffer controlled_buffer_2
  assign print_r = pr_in_prog ? ~pr_in_prog : 1'bz;  // Controlled_Inverter controlled_inverter_1
  S_R_Flip_Flop #(.trigger("falling")) s_r_ff_2 (
    .Q(print_done), .preset(pr_done), .reset(or_1_out));  // open: S, clk, R, Qn, en
  or or_1 (or_1_out, reset, pr_in_prog);

  // Notes on the sheet:
  //   sentinels
  //   cards
  //   if = 0x90
endmodule

module card_replace (
  input  [2:0] colod_number,
  input  [7:0] cur_command,
  output [7:0] updated_program,
  output move_done_updated
);

  wire _1st_done, _2st_done, and_1_out, and_2_out, and_3_out, and_4_out, and_5_out, and_6_out, and_7_out,
       and_8_out, colod_isnt_0, comparator_1_eq, not_equal, or_3_out, or_4_out;

  Comparator #(.width(3), .mode("unsigned")) comparator_1 (
    .a(colod_number), .b(3'b000), .eq(comparator_1_eq));  // open: gt, lt
  not not_1 (colod_isnt_0, comparator_1_eq);
  Comparator #(.width(3), .mode("unsigned")) comparator_2 (
    .a(colod_number), .b(cur_command[2:0]), .eq(not_equal));  // open: gt, lt
  or or_1 (_1st_done, cur_command[0], cur_command[1], cur_command[2], cur_command[3]);
  or or_2 (_2st_done, cur_command[4], cur_command[5], cur_command[6], cur_command[7]);
  and and_1 (and_1_out, _1st_done, _2st_done);
  or or_3 (or_3_out, updated_program[0], updated_program[1], updated_program[2], updated_program[3]);
  and and_2 (and_2_out, or_3_out, or_4_out);
  or or_4 (or_4_out, updated_program[4], updated_program[5], updated_program[6], updated_program[7]);
  or or_5 (move_done_updated, and_1_out, and_2_out);
  and and_3 (and_3_out, _1st_done, colod_isnt_0, _2st_done, ~not_equal);  // AND_Gate
  and and_4 (and_4_out, _1st_done, ~colod_isnt_0, _2st_done, ~not_equal);  // AND_Gate
  and and_5 (and_5_out, _1st_done, colod_isnt_0, ~_2st_done, ~not_equal);  // AND_Gate
  and and_6 (and_6_out, ~_1st_done, colod_isnt_0, ~_2st_done, ~not_equal);  // AND_Gate
  and and_7 (and_7_out, _1st_done, ~colod_isnt_0, ~_2st_done, ~not_equal);  // AND_Gate
  and and_8 (and_8_out, ~_1st_done, ~colod_isnt_0, ~_2st_done, ~not_equal);  // AND_Gate
  assign updated_program = and_3_out ? cur_command : 8'bz;  // Controlled_Buffer controlled_buffer_1
  assign updated_program = and_4_out ? cur_command : 8'bz;  // Controlled_Buffer controlled_buffer_2
  assign updated_program = and_5_out ? {1'b0, colod_number, cur_command[3:0]} : 8'bz;  // Controlled_Buffer controlled_buffer_3
  assign updated_program = and_6_out ? {cur_command[7:4], 1'b0, colod_number} : 8'bz;  // Controlled_Buffer controlled_buffer_4
  assign updated_program = and_7_out ? cur_command : 8'bz;  // Controlled_Buffer controlled_buffer_5
  assign updated_program = and_8_out ? cur_command : 8'bz;  // Controlled_Buffer controlled_buffer_6
  assign updated_program = not_equal ? cur_command : 8'bz;  // Controlled_Buffer controlled_buffer_7

  // Other names for the same wires on the sheet: c[2:0] = colod_number;
  //   case1 (some bits) = {cur_command[7:4], colod_number}; case2[6:0] = {colod_number, cur_command[3:0]};
  //   case3[7:0] = cur_command; command[7:0] = cur_command; res[7:0] = updated_program
endmodule

module my_replace (
  input  [3:0] colod_number,
  input  enable,
  input  clock,
  input  reset,
  output [7:0] from_to,
  output com_ready
);

  wire and_1_out, wr_done, wr_from, wr_in_prog;
  wire [3:0] demultiplexer_1_out0, demultiplexer_1_out1;

  S_R_Flip_Flop #(.trigger("falling")) s_r_ff_1 (
    .Q(wr_in_prog), .preset(and_1_out), .reset(wr_done));  // open: S, clk, R, Qn, en
  and and_1 (and_1_out, enable, ~com_ready);  // AND_Gate
  Demultiplexer #(.width(4), .tristate("true")) demultiplexer_1 (
    .out0(demultiplexer_1_out0), .out1(demultiplexer_1_out1), .in(colod_number), .sel(wr_from),
    .en(wr_in_prog));
  Register #(.width(4)) register_1 (.D(demultiplexer_1_out0), .Q(from_to[3:0]), .clk(clock), .clr(reset));  // open: en
  Register #(.width(4)) register_2 (.D(demultiplexer_1_out1), .Q(from_to[7:4]), .clk(clock), .clr(reset));  // open: en
  or or_1 (wr_from, from_to[0], from_to[1], from_to[2], from_to[3]);
  or or_2 (com_ready, from_to[4], from_to[5], from_to[6], from_to[7]);
  D_Flip_Flop d_ff_1 (.clk(clock), .D(wr_in_prog), .Q(wr_done));  // open: Qn, preset, en, reset

  // Other names for the same wires on the sheet: c[3:0] = colod_number; wr_stop = com_ready

  // Notes on the sheet:
  //   to column was written
  //   from column was written
endmodule

module write_offset (
  input  clock,
  input  reset,
  output [7:0] address,
  output [7:0] data,
  output ofs_done,
  output ofs_ld
);

  wire all_cols, not_1_out, ofs_done_t, ofs_in_prog, ofs_in_prog_prime, write_ofs;
  wire [2:0] counter_1_q;
  wire [7:0] addr, bit_extender_1_out, data_t;

  S_R_Flip_Flop #(.trigger("falling")) s_r_ff_1 (
    .Q(ofs_in_prog), .Qn(ofs_in_prog_prime), .preset(reset), .reset(ofs_done_t));  // open: S, clk, R, en
  Multiplexer #(.select(3), .width(8), .disabled(0), .enable("false")) multiplexer_1 (
    .in0(8'h90), .in1(8'h99), .in2(8'ha3), .in3(8'hae), .in4(8'hba), .in5(8'hc7), .in6(8'hd5), .out(data_t),
    .sel(counter_1_q));  // open: in7
  Counter #(.width(3), .max('h7)) counter_1 (
    .count(ofs_in_prog), .Q(counter_1_q), .clk(clock), .clr(reset));  // open: load, D, carry
  and and_1 (write_ofs, ~clock, ofs_in_prog);  // AND_Gate
  assign address = write_ofs ? addr : 8'bz;  // Controlled_Buffer controlled_buffer_1
  Comparator #(.width(3), .mode("unsigned")) comparator_1 (.a(3'b111), .b(counter_1_q), .eq(all_cols));  // open: gt, lt
  assign bit_extender_1_out = {{5{1'b0}}, counter_1_q};  // Bit_Extender bit_extender_1
  assign data = write_ofs ? data_t : 8'bz;  // Controlled_Buffer controlled_buffer_2
  Adder adder_1 (.a(8'h80), .b(bit_extender_1_out), .out(addr));  // open: cin, cout
  and and_2 (ofs_done_t, all_cols, ~clock);  // AND_Gate
  not not_1 (not_1_out, ofs_in_prog_prime);
  assign ofs_ld = ofs_in_prog ? write_ofs : 1'bz;  // Controlled_Buffer controlled_buffer_3
  and and_3 (ofs_done, ofs_in_prog_prime, not_1_out);
endmodule
